// Logisim project One-Hot to Nature.circ as structural Verilog: 1 circuit, main circuit One-Hot to Nature
module One_Hot_to_Nature (
  input  s4,
  input  s3,
  input  s2,
  input  s1,
  input  s0,
  output o3,
  output o2,
  output o1
);

  or or_1 (o2, s2, s3);
  or or_2 (o1, s1, s3);

  assign o3 = s4;
endmodule
