// Logisim project 分析复杂电路.circ as structural Verilog: 2 circuits, main circuit 分析复杂电路-电路功能分析
// a
module \分析复杂电路_电路功能分析  (
  input  a,
  input  b,
  input  c,
  output o1,
  output o2
);

  wire and_1_out, and_2_out, and_3_out, and_4_out, not_1_out, not_2_out;

  not not_1 (not_1_out, c);
  not not_2 (not_2_out, c);
  and and_1 (and_1_out, b, c);
  and and_2 (and_2_out, a, not_1_out);
  and and_3 (and_3_out, b, not_2_out);
  and and_4 (and_4_out, a, c);
  or or_1 (o1, and_1_out, and_1_out, and_2_out);
  or or_2 (o2, and_3_out, and_3_out, and_4_out, and_4_out);
endmodule

module \分析复杂电路_等价电路  (
  input  a,
  input  b,
  input  c,
  output y
);

  wire and_1_out, and_2_out, not_1_out, not_2_out, not_3_out, not_4_out, not_5_out, not_6_out, or_1_out,
       or_2_out;

  not not_1 (not_1_out, a);
  or or_1 (or_1_out, not_1_out, b, c);
  not not_2 (not_2_out, a);
  not not_3 (not_3_out, b);
  or or_2 (or_2_out, not_2_out, not_3_out, c);
  not not_4 (not_4_out, a);
  and and_1 (and_1_out, not_4_out, b, c);
  and and_2 (and_2_out, a, b, c);
  not not_5 (not_5_out, or_1_out);
  not not_6 (not_6_out, or_2_out);
  or or_3 (y, not_5_out, not_6_out, and_1_out, and_2_out);
endmodule
