// Logisim project 4位左移移位器.circ as structural Verilog: 1 circuit, main circuit main
module main (
  input  in_1,
  input  [3:0] in_2,
  input  [1:0] in_3,
  output [3:0] out_4
);

  wire [3:0] demultiplexer_1_out0, demultiplexer_1_out1, demultiplexer_2_out0, demultiplexer_2_out1, or_1_out;

  Demultiplexer #(.width(4), .enable("false")) demultiplexer_1 (
    .out0(demultiplexer_1_out0), .out1(demultiplexer_1_out1), .in(in_2), .sel(in_3[1]));
  // Probe on {demultiplexer_1_out1[1:0], {2{in_1}}}
  assign or_1_out = demultiplexer_1_out0 | {demultiplexer_1_out1[1:0], {2{in_1}}};  // OR_Gate or_1, 4 bits wide
  Demultiplexer #(.width(4), .enable("false")) demultiplexer_2 (
    .out0(demultiplexer_2_out0), .out1(demultiplexer_2_out1), .in(or_1_out), .sel(in_3[0]));
  // Probe on {demultiplexer_2_out1[2:0], in_1}
  assign out_4 = demultiplexer_2_out0 | {demultiplexer_2_out1[2:0], in_1};  // OR_Gate or_2, 4 bits wide
endmodule
