// Logisim project Fabonacci-32digit.circ as structural Verilog: 3 circuits, main circuit 三位到8位
module main (
  input  [2:0] in_1,
  output [31:0] out_2
);

  wire and_1_out, and_2_out, and_3_out, and_4_out, and_6_out, clock_1_out, comparator_1_eq, comparator_1_lt,
       not_1_out, not_2_out, not_3_out, not_4_out, not_5_out, not_6_out, or_1_out, or_2_out, s_r_ff_1_qn,
       s_r_ff_2_q, s_r_ff_2_qn, s_r_ff_3_q, s_r_ff_4_qn, stop;
  wire [7:0] counter_1_q, \三位到8位_1_out_2 ;
  wire [31:0] A_q, adder_1_out, and_7_out, and_8_out, B_q, C_q, controlled_buffer_1_out, not_7_out,
       \位扩展_1_out_2 ;

  Clock clock_1 (.out(clock_1_out));
  Counter counter_1 (.Q(counter_1_q), .clk(clock_1_out));  // open: load, D, count, carry, clr
  S_R_Flip_Flop s_r_ff_1 (.Qn(s_r_ff_1_qn), .preset(and_2_out));  // open: S, clk, R, Q, reset, en
  Comparator #(.mode("unsigned")) comparator_1 (
    .a(counter_1_q), .b(\三位到8位_1_out_2 ), .eq(comparator_1_eq), .lt(comparator_1_lt));  // open: gt
  \三位到8位  \u_三位到8位_1  (.in_1(in_1), .out_2(\三位到8位_1_out_2 ));
  S_R_Flip_Flop s_r_ff_2 (.Q(s_r_ff_2_q), .Qn(s_r_ff_2_qn), .preset(and_2_out));  // open: S, clk, R, reset, en
  S_R_Flip_Flop s_r_ff_3 (.Q(s_r_ff_3_q), .preset(and_2_out));  // open: S, clk, R, Qn, reset, en
  not not_1 (not_1_out, or_1_out);
  or or_1 (or_1_out, comparator_1_eq, comparator_1_lt);
  and and_1 (and_1_out, clock_1_out, s_r_ff_1_qn);
  and and_2 (and_2_out, not_4_out, not_2_out);
  not not_2 (not_2_out, not_4_out);
  and and_3 (and_3_out, clock_1_out, s_r_ff_3_q);
  not not_3 (not_3_out, not_1_out);
  and and_4 (and_4_out, not_3_out, not_1_out);
  not not_4 (not_4_out, and_1_out);
  not not_5 (not_5_out, and_3_out);
  not not_6 (not_6_out, not_5_out);
  S_R_Flip_Flop s_r_ff_4 (.Qn(s_r_ff_4_qn), .preset(and_4_out));  // open: S, clk, R, Q, reset, en
  and and_5 (stop, s_r_ff_4_qn, or_1_out);
  and and_6 (and_6_out, not_5_out, not_6_out);
  Pull_Resistor pull_resistor_1 (.node(and_3_out));
  Pull_Resistor pull_resistor_2 (.node(and_6_out));
  Pull_Resistor pull_resistor_3 (.node(and_6_out));
  or or_2 (or_2_out, and_1_out, and_6_out);
  assign controlled_buffer_1_out = s_r_ff_2_qn ? 32'h1 : 32'bz;  // Controlled_Buffer controlled_buffer_1
  assign controlled_buffer_1_out = s_r_ff_2_q ? B_q : 32'bz;  // Controlled_Buffer controlled_buffer_2
  Register #(.width(32)) A (.D(controlled_buffer_1_out), .Q(A_q), .clk(or_2_out));  // open: en, clr
  Register #(.width(32)) B (.D(C_q), .Q(B_q), .clk(and_6_out));  // open: en, clr
  Register #(.width(32)) C (.D(adder_1_out), .en(stop), .Q(C_q), .clk(and_3_out));  // open: clr
  Adder #(.width(32)) adder_1 (.a(A_q), .b(B_q), .out(adder_1_out));  // open: cin, cout
  \位扩展  \u_位扩展_1  (.in_1(stop), .out_2(\位扩展_1_out_2 ));
  // Probe on C_q
  assign and_7_out = C_q & not_7_out;  // AND_Gate and_7, 32 bits wide
  assign not_7_out = ~\位扩展_1_out_2 ;  // NOT_Gate not_7, 32 bits wide
  assign and_8_out = \位扩展_1_out_2  & {32{1'b0}};  // AND_Gate and_8, 32 bits wide
  assign out_2 = and_7_out | and_8_out;  // OR_Gate or_3, 32 bits wide
endmodule

module \三位到8位  (
  input  [2:0] in_1,
  output [7:0] out_2
);


  assign out_2 = {{5{1'b0}}, in_1};
endmodule

module \位扩展  (
  input  in_1,
  output [31:0] out_2
);


  assign out_2 = {32{in_1}};
endmodule
