// Logisim project Fibonacci-8digit.circ as structural Verilog: 3 circuits, main circuit main
module main (
  input  [2:0] in_1,
  output [3:0] out_2
);

  wire and_1_out, and_2_out, and_3_out, and_4_out, and_5_out, clock_1_out, comparator_1_eq, not_1_out,
       not_2_out, not_3_out, not_4_out, not_5_out, or_1_out, s_r_ff_1_qn, s_r_ff_2_q, s_r_ff_2_qn,
       s_r_ff_3_q, stop;
  wire [3:0] A_q, adder_1_out, and_6_out, and_7_out, B_q, C_q, controlled_buffer_1_out, counter_1_q,
       \n1位扩展4位_1_out_2 , \n3位扩展4位并加1_1_out_2 , not_6_out;

  Clock clock_1 (.out(clock_1_out));
  \_3位扩展4位并加1  \u_3位扩展4位并加1_1  (.in_1(in_1), .out_2(\n3位扩展4位并加1_1_out_2 ));
  Counter #(.width(4), .max('hf)) counter_1 (.Q(counter_1_q), .clk(clock_1_out));  // open: load, D, count, carry, clr
  Comparator #(.width(4), .mode("unsigned")) comparator_1 (
    .a(\n3位扩展4位并加1_1_out_2 ), .b(counter_1_q), .eq(comparator_1_eq));  // open: gt, lt
  S_R_Flip_Flop s_r_ff_1 (.Qn(s_r_ff_1_qn), .preset(and_2_out));  // open: S, clk, R, Q, reset, en
  not not_1 (not_1_out, comparator_1_eq);
  and and_1 (and_1_out, clock_1_out, s_r_ff_1_qn);
  and and_2 (and_2_out, not_2_out, not_3_out);
  S_R_Flip_Flop s_r_ff_2 (.Q(s_r_ff_2_q), .Qn(s_r_ff_2_qn), .preset(and_2_out));  // open: S, clk, R, reset, en
  S_R_Flip_Flop s_r_ff_3 (.Q(s_r_ff_3_q), .preset(and_2_out));  // open: S, clk, R, Qn, reset, en
  and and_3 (and_3_out, comparator_1_eq, not_1_out);
  not not_2 (not_2_out, and_1_out);
  not not_3 (not_3_out, not_2_out);
  and and_4 (and_4_out, clock_1_out, s_r_ff_3_q);
  and and_5 (and_5_out, not_5_out, not_4_out);
  not not_4 (not_4_out, not_5_out);
  S_R_Flip_Flop s_r_ff_4 (.Qn(stop), .preset(and_3_out));  // open: S, clk, R, Q, reset, en
  not not_5 (not_5_out, and_4_out);
  Pull_Resistor pull_resistor_1 (.node(and_5_out));
  Pull_Resistor pull_resistor_2 (.node(and_4_out));
  Pull_Resistor pull_resistor_3 (.node(and_5_out));
  or or_1 (or_1_out, and_1_out, and_5_out);
  assign controlled_buffer_1_out = s_r_ff_2_q ? B_q : 4'bz;  // Controlled_Buffer controlled_buffer_1
  assign controlled_buffer_1_out = s_r_ff_2_qn ? 4'b0001 : 4'bz;  // Controlled_Buffer controlled_buffer_2
  Register #(.width(4)) A (.D(controlled_buffer_1_out), .Q(A_q), .clk(or_1_out));  // open: en, clr
  Register #(.width(4)) B (.D(C_q), .Q(B_q), .clk(and_5_out));  // open: en, clr
  Register #(.width(4)) C (.D(adder_1_out), .en(stop), .Q(C_q), .clk(and_4_out));  // open: clr
  Adder #(.width(4)) adder_1 (.a(A_q), .b(B_q), .out(adder_1_out));  // open: cin, cout
  \_1位扩展4位  \u_1位扩展4位_1  (.in_1(stop), .out_2(\n1位扩展4位_1_out_2 ));
  assign not_6_out = ~\n1位扩展4位_1_out_2 ;  // NOT_Gate not_6, 4 bits wide
  assign and_6_out = C_q & not_6_out;  // AND_Gate and_6, 4 bits wide
  assign out_2 = and_6_out | and_7_out;  // OR_Gate or_2, 4 bits wide
  assign and_7_out = \n1位扩展4位_1_out_2  & 4'b0000;  // AND_Gate and_7, 4 bits wide
endmodule

module \_3位扩展4位并加1  (
  input  [2:0] in_1,
  output [3:0] out_2
);

  Adder #(.width(4)) adder_1 (.a({1'b0, in_1}), .b(4'b0001), .out(out_2));  // open: cin, cout
endmodule

module \_1位扩展4位  (
  input  in_1,
  output [3:0] out_2
);


  assign out_2 = {4{in_1}};
endmodule
