// Logisim project Fibonacci-Youtube.circ as structural Verilog: 4 circuits, main circuit main
module main (
  input  in_1
);

  wire and_1_out, and_2_out, and_3_out, clock_1_out, controlled_buffer_2_out, controlled_buffer_3_out,
       controlled_buffer_4_out, controlled_buffer_5_out, controlled_buffer_6_out, controlled_buffer_7_out,
       counter_1_q, demultiplexer_1_out0, demultiplexer_1_out1, demultiplexer_2_out0, demultiplexer_2_out1,
       demultiplexer_2_out2, not_1_out, not_2_out, not_3_out, not_4_out, s_r_ff_1_qn, s_r_ff_2_q, s_r_ff_3_q,
       s_r_ff_3_qn;
  wire [1:0] counter_2_q;
  wire [31:0] A_q, adder_1_out, B_q, C_q, controlled_buffer_9_out;

  Clock clock_1 (.out(clock_1_out));
  S_R_Flip_Flop s_r_ff_1 (.Qn(s_r_ff_1_qn), .preset(and_3_out));  // open: S, clk, R, Q, reset
  and and_1 (and_1_out, clock_1_out, s_r_ff_2_q);
  S_R_Flip_Flop s_r_ff_2 (.Q(s_r_ff_2_q), .preset(and_3_out));  // open: S, clk, R, Qn, reset
  and and_2 (and_2_out, clock_1_out, s_r_ff_1_qn);
  not not_1 (not_1_out, and_2_out);
  Controlled_Buffer controlled_buffer_1 (.in(in_1), .en(in_1));  // open: out
  Demultiplexer #(.enable("false")) demultiplexer_1 (
    .out0(demultiplexer_1_out0), .out1(demultiplexer_1_out1), .in(and_1_out), .sel(counter_1_q));
  Counter #(.width(1), .max('h1)) counter_1 (
    .Q(counter_1_q), .clk(not_2_out));  // open: load, D, count, carry, clr, preset, down
  not not_2 (not_2_out, and_1_out);
  Demultiplexer #(.select(2), .enable("false")) demultiplexer_2 (
    .out0(demultiplexer_2_out0), .out1(demultiplexer_2_out1), .out2(demultiplexer_2_out2), .in(and_2_out),
    .sel(counter_2_q));  // open: out3
  Counter #(.width(2), .max('h3)) counter_2 (
    .Q(counter_2_q), .clk(not_1_out));  // open: load, D, count, carry, clr, preset, down
  and and_3 (and_3_out, not_4_out, not_3_out);
  not not_3 (not_3_out, not_4_out);
  assign controlled_buffer_2_out = demultiplexer_2_out0 ? demultiplexer_2_out0 : 1'bz;  // Controlled_Buffer controlled_buffer_2
  assign controlled_buffer_3_out = demultiplexer_2_out0 ? demultiplexer_2_out0 : 1'bz;  // Controlled_Buffer controlled_buffer_3
  assign controlled_buffer_4_out = demultiplexer_2_out1 ? demultiplexer_2_out1 : 1'bz;  // Controlled_Buffer controlled_buffer_4
  assign controlled_buffer_5_out = demultiplexer_2_out2 ? demultiplexer_2_out2 : 1'bz;  // Controlled_Buffer controlled_buffer_5
  not not_4 (not_4_out, demultiplexer_2_out2);
  assign controlled_buffer_6_out = demultiplexer_1_out0 ? demultiplexer_1_out0 : 1'bz;  // Controlled_Buffer controlled_buffer_6
  assign controlled_buffer_7_out = demultiplexer_1_out1 ? demultiplexer_1_out1 : 1'bz;  // Controlled_Buffer controlled_buffer_7
  assign controlled_buffer_4_out = demultiplexer_1_out1 ? demultiplexer_1_out1 : 1'bz;  // Controlled_Buffer controlled_buffer_8
  Pull_Resistor pull_resistor_1 (.node(controlled_buffer_6_out));
  Pull_Resistor pull_resistor_2 (.node(controlled_buffer_4_out));
  Pull_Resistor pull_resistor_3 (.node(controlled_buffer_7_out));
  Pull_Resistor pull_resistor_4 (.node(controlled_buffer_3_out));
  Pull_Resistor pull_resistor_5 (.node(controlled_buffer_5_out));
  Pull_Resistor pull_resistor_6 (.node(controlled_buffer_2_out));
  Button \A置0  ();  // open: out
  Button \A导入  ();  // open: out
  Button \B导入  ();  // open: out
  Button \C导入  ();  // open: out
  Button \u_给B常量线路  ();  // open: out
  Button \u_选C导入B线路  ();  // open: out
  assign controlled_buffer_9_out = s_r_ff_3_qn ? 32'h1 : 32'bz;  // Controlled_Buffer controlled_buffer_9
  S_R_Flip_Flop s_r_ff_3 (
    .Q(s_r_ff_3_q), .Qn(s_r_ff_3_qn), .preset(controlled_buffer_5_out), .reset(controlled_buffer_3_out));  // open: S, clk, R
  assign controlled_buffer_9_out = s_r_ff_3_q ? C_q : 32'bz;  // Controlled_Buffer controlled_buffer_10
  Register #(.width(32), .Select("low")) A (
    .D(B_q), .Q(A_q), .clk(controlled_buffer_7_out), .clr(controlled_buffer_2_out));  // open: en
  Register #(.width(32), .Select("low")) B (
    .D(controlled_buffer_9_out), .Q(B_q), .clk(controlled_buffer_4_out));  // open: en, clr
  Register #(.width(32), .Select("low")) C (.D(adder_1_out), .Q(C_q), .clk(controlled_buffer_6_out));  // open: en, clr
  // Probe on A_q
  // Probe on B_q
  // Probe on adder_1_out
  // Probe on C_q
  Adder #(.width(32)) adder_1 (.a(A_q), .b(B_q), .out(adder_1_out));  // open: cin, cout
endmodule

module Fibonacci (
  input  [2:0] in_1,
  input  in_2
);

  wire and_1_out, and_2_out, and_3_out, and_4_out, button_1_out, clock_1_out, comparator_1_lt,
       controlled_buffer_1_out, controlled_buffer_3_out, controlled_buffer_5_out, controlled_buffer_6_out,
       counter_3_q, demultiplexer_1_out0, demultiplexer_1_out1, demultiplexer_1_out2, demultiplexer_2_out0,
       demultiplexer_2_out1, not_1_out, not_2_out, not_3_out, not_4_out, pull_resistor_1_node,
       pull_resistor_2_node, s_r_ff_2_q, s_r_ff_3_q, s_r_ff_4_q, s_r_ff_4_qn;
  wire [1:0] counter_2_q;
  wire [2:0] counter_1_q;
  wire [31:0] A_q, adder_1_out, B_q, C_q, controlled_buffer_8_out;

  Clock clock_1 (.out(clock_1_out));
  Counter #(.width(3), .max('h7)) counter_1 (
    .Q(counter_1_q), .clk(clock_1_out));  // open: load, D, count, carry, clr, preset, down
  and and_1 (and_1_out, clock_1_out, comparator_1_lt);
  Button button_1 (.out(button_1_out));
  Comparator #(.width(3), .mode("unsigned")) comparator_1 (
    .a(counter_1_q), .b(in_1), .lt(comparator_1_lt));  // open: gt, eq
  S_R_Flip_Flop s_r_ff_1 (.preset(1'b1), .reset(in_2));  // open: S, clk, R, Q, Qn
  S_R_Flip_Flop s_r_ff_2 (.Q(s_r_ff_2_q), .preset(button_1_out), .reset(and_4_out));  // open: S, clk, R, Qn
  S_R_Flip_Flop s_r_ff_3 (.Q(s_r_ff_3_q), .preset(and_4_out), .reset(button_1_out));  // open: S, clk, R, Qn
  and and_2 (and_2_out, and_1_out, s_r_ff_2_q);
  and and_3 (and_3_out, and_1_out, s_r_ff_3_q);
  not not_1 (not_1_out, and_3_out);
  Demultiplexer #(.select(2), .enable("false")) demultiplexer_1 (
    .out0(demultiplexer_1_out0), .out1(demultiplexer_1_out1), .out2(demultiplexer_1_out2), .in(and_2_out),
    .sel(counter_2_q));  // open: out3
  Counter #(.width(2), .max('h3)) counter_2 (
    .Q(counter_2_q), .clk(not_2_out), .clr(button_1_out));  // open: load, D, count, carry, preset, down
  not not_2 (not_2_out, and_2_out);
  and and_4 (and_4_out, not_3_out, not_4_out);
  Demultiplexer #(.enable("false")) demultiplexer_2 (
    .out0(demultiplexer_2_out0), .out1(demultiplexer_2_out1), .in(and_3_out), .sel(counter_3_q));
  Counter #(.width(1), .max('h1)) counter_3 (
    .Q(counter_3_q), .clk(not_1_out), .clr(button_1_out));  // open: load, D, count, carry, preset, down
  not not_3 (not_3_out, demultiplexer_1_out2);
  not not_4 (not_4_out, not_3_out);
  Pull_Resistor pull_resistor_1 (.node(pull_resistor_1_node));
  Pull_Resistor pull_resistor_2 (.node(pull_resistor_2_node));
  assign controlled_buffer_1_out = demultiplexer_1_out0 ? demultiplexer_1_out0 : 1'bz;  // Controlled_Buffer controlled_buffer_1
  assign pull_resistor_1_node = demultiplexer_1_out0 ? demultiplexer_1_out0 : 1'bz;  // Controlled_Buffer controlled_buffer_2
  assign controlled_buffer_3_out = demultiplexer_1_out1 ? demultiplexer_1_out1 : 1'bz;  // Controlled_Buffer controlled_buffer_3
  assign pull_resistor_2_node = demultiplexer_1_out2 ? demultiplexer_1_out2 : 1'bz;  // Controlled_Buffer controlled_buffer_4
  assign controlled_buffer_5_out = demultiplexer_2_out0 ? demultiplexer_2_out0 : 1'bz;  // Controlled_Buffer controlled_buffer_5
  assign controlled_buffer_6_out = demultiplexer_2_out1 ? demultiplexer_2_out1 : 1'bz;  // Controlled_Buffer controlled_buffer_6
  assign controlled_buffer_3_out = demultiplexer_2_out1 ? demultiplexer_2_out1 : 1'bz;  // Controlled_Buffer controlled_buffer_7
  Pull_Resistor pull_resistor_3 (.node(controlled_buffer_6_out));
  Pull_Resistor pull_resistor_4 (.node(controlled_buffer_1_out));
  Pull_Resistor pull_resistor_5 (.node(controlled_buffer_5_out));
  Pull_Resistor pull_resistor_6 (.node(controlled_buffer_3_out));
  S_R_Flip_Flop s_r_ff_4 (
    .Q(s_r_ff_4_q), .Qn(s_r_ff_4_qn), .preset(pull_resistor_2_node), .reset(pull_resistor_1_node));  // open: S, clk, R
  Button \A置0  ();  // open: out
  Button \A导入  ();  // open: out
  Button \B导入  ();  // open: out
  Button \C导入  ();  // open: out
  Button \u_给B常量线路  ();  // open: out
  Button \u_选C导入B线路  ();  // open: out
  assign controlled_buffer_8_out = s_r_ff_4_qn ? 32'h1 : 32'bz;  // Controlled_Buffer controlled_buffer_8
  assign controlled_buffer_8_out = s_r_ff_4_q ? C_q : 32'bz;  // Controlled_Buffer controlled_buffer_9
  Register #(.width(32), .Select("low")) A (
    .D(B_q), .Q(A_q), .clk(controlled_buffer_6_out), .clr(controlled_buffer_1_out));  // open: en
  Register #(.width(32), .Select("low")) B (
    .D(controlled_buffer_8_out), .Q(B_q), .clk(controlled_buffer_3_out));  // open: en, clr
  Register #(.width(32), .Select("low")) C (.D(adder_1_out), .Q(C_q), .clk(controlled_buffer_5_out));  // open: en, clr
  // Probe on A_q
  // Probe on B_q
  // Probe on adder_1_out
  Adder #(.width(32)) adder_1 (.a(A_q), .b(B_q), .out(adder_1_out));  // open: cin, cout
endmodule

module test (
  input  [2:0] in_1
);

  wire and_1_out, and_2_out, and_3_out, and_4_out, and_5_out, clock_1_out, comparator_1_eq, comparator_1_lt,
       controlled_buffer_1_out, controlled_buffer_2_out, controlled_buffer_3_out, controlled_buffer_4_out,
       controlled_buffer_5_out, controlled_buffer_6_out, counter_1_q, counter_3_q, counter_4_q,
       demultiplexer_1_out0, demultiplexer_1_out1, demultiplexer_2_out0, demultiplexer_2_out1,
       demultiplexer_2_out2, not_1_out, not_2_out, not_3_out, not_4_out, not_5_out, not_6_out, s_r_ff_1_q,
       s_r_ff_2_q, s_r_ff_3_q, s_r_ff_4_q, s_r_ff_4_qn, undriven;
  wire [1:0] counter_5_q;
  wire [3:0] adder_1_out, counter_2_q, myfab_1_p2;
  wire [31:0] A_q, adder_2_out, B_q, C_q, controlled_buffer_8_out;

  S_R_Flip_Flop s_r_ff_1 (.Q(s_r_ff_1_q), .preset(1'b1), .reset(counter_1_q));  // open: S, clk, R, Qn
  Counter #(.width(1), .max('h1)) counter_1 (
    .Q(counter_1_q), .clk(and_1_out));  // open: load, D, count, carry, clr, preset, down
  Clock clock_1 (.out(clock_1_out));
  Counter #(.width(4), .max('hf)) counter_2 (
    .Q(counter_2_q), .clk(clock_1_out));  // open: load, D, count, carry, clr, preset, down
  and and_1 (and_1_out, not_2_out, not_1_out);
  not not_1 (not_1_out, not_2_out);
  Adder #(.width(4)) adder_1 (.a(4'b0010), .b(counter_2_q), .out(adder_1_out));  // open: cin, cout
  // MyFab myfab_1: pin names not known; wires that end beside it: in_1, myfab_1_p2
  // Probe on myfab_1_p2
  not not_2 (not_2_out, comparator_1_eq);
  and and_2 (and_2_out, clock_1_out, s_r_ff_1_q, comparator_1_lt);
  Comparator #(.width(4), .mode("unsigned")) comparator_1 (
    .a(adder_1_out), .b(myfab_1_p2), .eq(comparator_1_eq), .lt(comparator_1_lt));  // open: gt
  Counter #(.width(1), .max('h1)) counter_3 (
    .Q(counter_3_q), .clk(and_5_out));  // open: load, D, count, carry, clr, preset, down
  S_R_Flip_Flop s_r_ff_2 (.Q(s_r_ff_2_q), .preset(1'b1), .reset(counter_3_q));  // open: S, clk, R, Qn
  and and_3 (and_3_out, and_2_out, s_r_ff_3_q);
  S_R_Flip_Flop s_r_ff_3 (.Q(s_r_ff_3_q), .preset(and_5_out), .reset(undriven));  // open: S, clk, R, Qn
  and and_4 (and_4_out, and_2_out, s_r_ff_2_q);
  not not_3 (not_3_out, and_4_out);
  Demultiplexer #(.enable("false")) demultiplexer_1 (
    .out0(demultiplexer_1_out0), .out1(demultiplexer_1_out1), .in(and_3_out), .sel(counter_4_q));
  not not_4 (not_4_out, and_3_out);
  Counter #(.width(1), .max('h1)) counter_4 (
    .Q(counter_4_q), .clk(not_4_out), .clr(undriven));  // open: load, D, count, carry, preset, down
  Demultiplexer #(.select(2), .enable("false")) demultiplexer_2 (
    .out0(demultiplexer_2_out0), .out1(demultiplexer_2_out1), .out2(demultiplexer_2_out2), .in(and_4_out),
    .sel(counter_5_q));  // open: out3
  Counter #(.width(2), .max('h3)) counter_5 (
    .Q(counter_5_q), .clk(not_3_out), .clr(undriven));  // open: load, D, count, carry, preset, down
  and and_5 (and_5_out, not_6_out, not_5_out);
  not not_5 (not_5_out, not_6_out);
  assign controlled_buffer_1_out = demultiplexer_2_out0 ? demultiplexer_2_out0 : 1'bz;  // Controlled_Buffer controlled_buffer_1
  assign controlled_buffer_2_out = demultiplexer_2_out0 ? demultiplexer_2_out0 : 1'bz;  // Controlled_Buffer controlled_buffer_2
  assign controlled_buffer_3_out = demultiplexer_2_out1 ? demultiplexer_2_out1 : 1'bz;  // Controlled_Buffer controlled_buffer_3
  assign controlled_buffer_4_out = demultiplexer_2_out2 ? demultiplexer_2_out2 : 1'bz;  // Controlled_Buffer controlled_buffer_4
  not not_6 (not_6_out, demultiplexer_2_out2);
  assign controlled_buffer_5_out = demultiplexer_1_out0 ? demultiplexer_1_out0 : 1'bz;  // Controlled_Buffer controlled_buffer_5
  assign controlled_buffer_6_out = demultiplexer_1_out1 ? demultiplexer_1_out1 : 1'bz;  // Controlled_Buffer controlled_buffer_6
  assign controlled_buffer_3_out = demultiplexer_1_out1 ? demultiplexer_1_out1 : 1'bz;  // Controlled_Buffer controlled_buffer_7
  Pull_Resistor pull_resistor_1 (.node(controlled_buffer_2_out));
  Pull_Resistor pull_resistor_2 (.node(controlled_buffer_6_out));
  Pull_Resistor pull_resistor_3 (.node(controlled_buffer_1_out));
  Pull_Resistor pull_resistor_4 (.node(controlled_buffer_3_out));
  Pull_Resistor pull_resistor_5 (.node(controlled_buffer_4_out));
  Pull_Resistor pull_resistor_6 (.node(controlled_buffer_5_out));
  Button \A置0  ();  // open: out
  Button \A导入  ();  // open: out
  Button \B导入  ();  // open: out
  Button \C导入  ();  // open: out
  Button \u_给B常量线路  ();  // open: out
  Button \u_选C导入B线路  ();  // open: out
  assign controlled_buffer_8_out = s_r_ff_4_qn ? 32'h1 : 32'bz;  // Controlled_Buffer controlled_buffer_8
  S_R_Flip_Flop s_r_ff_4 (
    .Q(s_r_ff_4_q), .Qn(s_r_ff_4_qn), .preset(controlled_buffer_4_out), .reset(controlled_buffer_2_out));  // open: S, clk, R
  assign controlled_buffer_8_out = s_r_ff_4_q ? C_q : 32'bz;  // Controlled_Buffer controlled_buffer_9
  Register #(.width(32), .Select("low")) A (
    .D(B_q), .Q(A_q), .clk(controlled_buffer_6_out), .clr(controlled_buffer_1_out));  // open: en
  Register #(.width(32), .Select("low")) B (
    .D(controlled_buffer_8_out), .Q(B_q), .clk(controlled_buffer_3_out));  // open: en, clr
  Register #(.width(32), .Select("low")) C (.D(adder_2_out), .Q(C_q), .clk(controlled_buffer_5_out));  // open: en, clr
  // Probe on A_q
  // Probe on B_q
  // Probe on adder_2_out
  Adder #(.width(32)) adder_2 (.a(A_q), .b(B_q), .out(adder_2_out));  // open: cin, cout
  // Probe on C_q
endmodule

module MyFab (
  input  in_1
);

  wire and_1_out, and_2_out, clock_1_out, not_1_out, not_2_out, s_r_ff_1_q, s_r_ff_1_qn;
  wire [7:0] A_q, adder_1_out, B_q, C_q, controlled_buffer_1_out;

  Clock clock_1 (.out(clock_1_out));
  not not_1 (not_1_out, clock_1_out);
  not not_2 (not_2_out, not_1_out);
  and and_1 (and_1_out, not_2_out, not_1_out);
  S_R_Flip_Flop s_r_ff_1 (.Q(s_r_ff_1_q), .Qn(s_r_ff_1_qn), .preset(and_1_out));  // open: S, clk, R, reset
  and and_2 (and_2_out, clock_1_out, s_r_ff_1_qn);
  // AND_Gate and_3 has open pins: in0=s_r_ff_1_q, in1=clock_1_out, out=open
  assign controlled_buffer_1_out = and_2_out ? 8'h1 : 8'bz;  // Controlled_Buffer controlled_buffer_1
  assign controlled_buffer_1_out = in_1 ? B_q : 8'bz;  // Controlled_Buffer controlled_buffer_2
  Register #(.Select("low")) A (.D(controlled_buffer_1_out), .Q(A_q), .clk(and_2_out));  // open: en, clr
  Register #(.Select("low")) B (.D(C_q), .Q(B_q));  // open: en, clk, clr
  Register #(.Select("low")) C (.D(adder_1_out), .Q(C_q));  // open: en, clk, clr
  Adder adder_1 (.a(A_q), .b(B_q), .out(adder_1_out));  // open: cin, cout
endmodule
