// Logisim project Fibonacci-快速幂.circ as structural Verilog: 4 circuits, main circuit Matrix self
module main (
  input  [31:0] in_1,
  output [31:0] out_2
);

  wire and_1_out, and_2_out, and_3_out, and_4_out, and_5_out, and_6_out, and_7_out, and_8_out, ati,
       clock_1_out, counter_1_carry, not_1_out, not_2_out, not_3_out, not_4_out, not_5_out, not_6_out,
       not_7_out, not_8_out, or_1_out, or_2_out, s_r_ff_1_q, s_r_ff_1_qn, s_r_ff_2_q, s_r_ff_2_qn,
       s_r_ff_3_q, s_r_ff_3_qn, s_r_ff_5_qn, stop;
  wire [4:0] counter_1_q;
  wire [31:0] and_9_out, and_10_out, controlled_buffer_1_out, controlled_buffer_3_out,
       controlled_buffer_5_out, controlled_buffer_7_out, controlled_buffer_9_out, controlled_buffer_11_out,
       controlled_buffer_13_out, controlled_buffer_15_out, matrix_self_1_out_5, matrix_self_1_out_6,
       matrix_self_1_out_7, matrix_self_1_out_8, muti_1_1, muti_1_2, muti_2_1, muti_2_2, n1to32bit_1_out_2,
       not_9_out, register_2_q, register_3_q, register_5_q, register_6_q, res_1_1, res_1_2, res_2_1, res_2_2;

  Clock clock_1 (.out(clock_1_out));
  S_R_Flip_Flop s_r_ff_1 (.Q(s_r_ff_1_q), .Qn(s_r_ff_1_qn), .preset(and_2_out));  // open: S, clk, R, reset, en
  and and_1 (and_1_out, clock_1_out, s_r_ff_1_qn);
  and and_2 (and_2_out, not_2_out, not_3_out);
  and and_3 (and_3_out, s_r_ff_1_q, clock_1_out);
  not not_1 (not_1_out, and_3_out);
  not not_2 (not_2_out, and_1_out);
  not not_3 (not_3_out, not_2_out);
  not not_4 (not_4_out, not_1_out);
  and and_4 (and_4_out, not_4_out, not_1_out);
  BitSelector #(.width(32)) bitselector_1 (.in(in_1), .out(ati), .sel(counter_1_q));
  Counter #(.width(5), .max('h1f)) counter_1 (
    .Q(counter_1_q), .carry(counter_1_carry), .clk(and_4_out));  // open: load, D, count, clr
  // Probe on counter_1_q
  not not_5 (not_5_out, counter_1_carry);
  not not_6 (not_6_out, not_5_out);
  or or_1 (or_1_out, and_1_out, and_3_out);
  and and_5 (and_5_out, not_5_out, not_6_out);
  S_R_Flip_Flop s_r_ff_2 (.Q(s_r_ff_2_q), .Qn(s_r_ff_2_qn), .preset(and_2_out));  // open: S, clk, R, reset, en
  S_R_Flip_Flop s_r_ff_3 (.Q(s_r_ff_3_q), .Qn(s_r_ff_3_qn), .preset(and_2_out));  // open: S, clk, R, reset, en
  S_R_Flip_Flop s_r_ff_4 (.Qn(stop), .preset(and_5_out));  // open: S, clk, R, Q, reset, en
  not not_7 (not_7_out, or_1_out);
  not not_8 (not_8_out, not_7_out);
  // Probe on controlled_buffer_1_out
  assign controlled_buffer_1_out = s_r_ff_2_q ? matrix_self_1_out_5 : 32'bz;  // Controlled_Buffer controlled_buffer_1
  assign controlled_buffer_1_out = s_r_ff_2_qn ? 32'h1 : 32'bz;  // Controlled_Buffer controlled_buffer_2
  S_R_Flip_Flop s_r_ff_5 (.Qn(s_r_ff_5_qn), .preset(and_6_out));  // open: S, clk, R, Q, reset, en
  and and_6 (and_6_out, not_7_out, not_8_out);
  assign controlled_buffer_3_out = s_r_ff_3_q ? res_1_1 : 32'bz;  // Controlled_Buffer controlled_buffer_3
  assign controlled_buffer_3_out = s_r_ff_3_qn ? 32'h1 : 32'bz;  // Controlled_Buffer controlled_buffer_4
  _1to32bit u_1to32bit_1 (.in_1(stop), .out_2(n1to32bit_1_out_2));
  // Probe on muti_1_1
  // Probe on muti_2_1
  assign controlled_buffer_5_out = s_r_ff_2_q ? matrix_self_1_out_6 : 32'bz;  // Controlled_Buffer controlled_buffer_5
  assign controlled_buffer_5_out = s_r_ff_2_qn ? 32'h1 : 32'bz;  // Controlled_Buffer controlled_buffer_6
  assign controlled_buffer_7_out = s_r_ff_3_q ? res_2_1 : 32'bz;  // Controlled_Buffer controlled_buffer_7
  assign controlled_buffer_7_out = s_r_ff_3_qn ? 32'h1 : 32'bz;  // Controlled_Buffer controlled_buffer_8
  // Probe on muti_1_2
  // Probe on muti_2_2
  assign controlled_buffer_9_out = s_r_ff_2_q ? matrix_self_1_out_7 : 32'bz;  // Controlled_Buffer controlled_buffer_9
  assign controlled_buffer_9_out = s_r_ff_2_qn ? 32'h1 : 32'bz;  // Controlled_Buffer controlled_buffer_10
  and and_7 (and_7_out, or_1_out, s_r_ff_5_qn);
  and and_8 (and_8_out, and_3_out, ati, stop);
  assign controlled_buffer_11_out = s_r_ff_3_q ? res_1_2 : 32'bz;  // Controlled_Buffer controlled_buffer_11
  assign controlled_buffer_11_out = s_r_ff_3_qn ? 32'h1 : 32'bz;  // Controlled_Buffer controlled_buffer_12
  assign controlled_buffer_13_out = s_r_ff_2_q ? matrix_self_1_out_8 : 32'bz;  // Controlled_Buffer controlled_buffer_13
  assign controlled_buffer_13_out = s_r_ff_2_qn ? {32{1'b0}} : 32'bz;  // Controlled_Buffer controlled_buffer_14
  or or_2 (or_2_out, and_7_out, and_8_out);
  assign controlled_buffer_15_out = s_r_ff_3_q ? res_2_2 : 32'bz;  // Controlled_Buffer controlled_buffer_15
  assign controlled_buffer_15_out = s_r_ff_3_qn ? {32{1'b0}} : 32'bz;  // Controlled_Buffer controlled_buffer_16
  Register #(.width(32)) register_1 (.D(controlled_buffer_1_out), .Q(muti_1_1), .clk(or_1_out));  // open: en, clr
  Register #(.width(32)) register_2 (.D(controlled_buffer_3_out), .Q(register_2_q), .clk(or_2_out));  // open: en, clr
  Register #(.width(32)) register_3 (.D(controlled_buffer_7_out), .Q(register_3_q), .clk(or_2_out));  // open: en, clr
  Register #(.width(32)) register_4 (.D(controlled_buffer_5_out), .Q(muti_2_1), .clk(or_1_out));  // open: en, clr
  Register #(.width(32)) register_5 (.D(controlled_buffer_11_out), .Q(register_5_q), .clk(or_2_out));  // open: en, clr
  Register #(.width(32)) register_6 (.D(controlled_buffer_15_out), .Q(register_6_q), .clk(or_2_out));  // open: en, clr
  Register #(.width(32)) register_7 (.D(controlled_buffer_9_out), .Q(muti_1_2), .clk(or_1_out));  // open: en, clr
  Register #(.width(32)) register_8 (.D(controlled_buffer_13_out), .Q(muti_2_2), .clk(or_1_out));  // open: en, clr
  assign not_9_out = ~n1to32bit_1_out_2;  // NOT_Gate not_9, 32 bits wide
  Matrix_self matrix_self_1 (
    ._1_1(muti_1_1), ._2_1(muti_2_1), ._1_2(muti_1_2), ._2_2(muti_2_2), .out_5(matrix_self_1_out_5),
    .out_6(matrix_self_1_out_6), .out_7(matrix_self_1_out_7), .out_8(matrix_self_1_out_8));
  // Probe on muti_1_1
  // Probe on muti_1_2
  assign and_9_out = register_6_q & not_9_out;  // AND_Gate and_9, 32 bits wide
  assign and_10_out = n1to32bit_1_out_2 & {32{1'b0}};  // AND_Gate and_10, 32 bits wide
  Matrix_x_times_y matrix_x_times_y_1 (
    .x_1_1(register_2_q), .x_2_1(register_3_q), .x_1_2(register_5_q), .x_2_2(register_6_q), .y_1_1(muti_1_1),
    .y_2_1(muti_2_1), .y_1_2(muti_1_2), .y_2_2(muti_2_2), .out_9(res_1_1), .out_10(res_2_1),
    .out_11(res_1_2), .out_12(res_2_2));
  assign out_2 = and_9_out | and_10_out;  // OR_Gate or_3, 32 bits wide
  // Probe on muti_2_1
  // Probe on muti_2_2
  // Probe on register_6_q
endmodule

module Matrix_self (
  input  [31:0] _1_1,
  input  [31:0] _2_1,
  input  [31:0] _1_2,
  input  [31:0] _2_2,
  output [31:0] out_5,
  output [31:0] out_6,
  output [31:0] out_7,
  output [31:0] out_8
);

  wire [31:0] multiplier_1_out, multiplier_2_out, multiplier_3_out, multiplier_4_out, multiplier_5_out,
       multiplier_6_out, multiplier_7_out, multiplier_8_out;

  Multiplier #(.width(32)) multiplier_1 (.a(_1_1), .b(_1_1), .out(multiplier_1_out));  // open: cin, cout
  Multiplier #(.width(32)) multiplier_2 (.a(_1_2), .b(_2_1), .out(multiplier_2_out));  // open: cin, cout
  Multiplier #(.width(32)) multiplier_3 (.a(_1_1), .b(_2_1), .out(multiplier_3_out));  // open: cin, cout
  Multiplier #(.width(32)) multiplier_4 (.a(_2_2), .b(_2_1), .out(multiplier_4_out));  // open: cin, cout
  Multiplier #(.width(32)) multiplier_5 (.a(_1_1), .b(_1_2), .out(multiplier_5_out));  // open: cin, cout
  Multiplier #(.width(32)) multiplier_6 (.a(_2_2), .b(_1_2), .out(multiplier_6_out));  // open: cin, cout
  Multiplier #(.width(32)) multiplier_7 (.a(_1_2), .b(_2_1), .out(multiplier_7_out));  // open: cin, cout
  Multiplier #(.width(32)) multiplier_8 (.a(_2_2), .b(_2_2), .out(multiplier_8_out));  // open: cin, cout
  Adder #(.width(32)) adder_1 (.a(multiplier_1_out), .b(multiplier_2_out), .out(out_5));  // open: cin, cout
  Adder #(.width(32)) adder_2 (.a(multiplier_3_out), .b(multiplier_4_out), .out(out_6));  // open: cin, cout
  Adder #(.width(32)) adder_3 (.a(multiplier_5_out), .b(multiplier_6_out), .out(out_7));  // open: cin, cout
  Adder #(.width(32)) adder_4 (.a(multiplier_7_out), .b(multiplier_8_out), .out(out_8));  // open: cin, cout

  // Other names for the same wires on the sheet: a[31:0] = _1_1; b[31:0] = _1_2; c[31:0] = _2_1; d[31:0] = _2_2
endmodule

module Matrix_x_times_y (
  input  [31:0] x_1_1,
  input  [31:0] x_2_1,
  input  [31:0] x_1_2,
  input  [31:0] x_2_2,
  input  [31:0] y_1_1,
  input  [31:0] y_2_1,
  input  [31:0] y_1_2,
  input  [31:0] y_2_2,
  output [31:0] out_9,
  output [31:0] out_10,
  output [31:0] out_11,
  output [31:0] out_12
);

  wire [31:0] multiplier_1_out, multiplier_2_out, multiplier_3_out, multiplier_4_out, multiplier_5_out,
       multiplier_6_out, multiplier_7_out, multiplier_8_out;

  Multiplier #(.width(32)) multiplier_1 (.a(x_1_1), .b(y_1_1), .out(multiplier_1_out));  // open: cin, cout
  Multiplier #(.width(32)) multiplier_2 (.a(x_1_2), .b(y_2_1), .out(multiplier_2_out));  // open: cin, cout
  Multiplier #(.width(32)) multiplier_3 (.a(x_2_1), .b(y_1_1), .out(multiplier_3_out));  // open: cin, cout
  Multiplier #(.width(32)) multiplier_4 (.a(x_2_2), .b(y_2_1), .out(multiplier_4_out));  // open: cin, cout
  Multiplier #(.width(32)) multiplier_5 (.a(x_1_1), .b(y_1_2), .out(multiplier_5_out));  // open: cin, cout
  Multiplier #(.width(32)) multiplier_6 (.a(x_1_2), .b(y_2_2), .out(multiplier_6_out));  // open: cin, cout
  Multiplier #(.width(32)) multiplier_7 (.a(x_2_1), .b(y_1_2), .out(multiplier_7_out));  // open: cin, cout
  Multiplier #(.width(32)) multiplier_8 (.a(x_2_2), .b(y_2_2), .out(multiplier_8_out));  // open: cin, cout
  Adder #(.width(32)) adder_1 (.a(multiplier_1_out), .b(multiplier_2_out), .out(out_9));  // open: cin, cout
  Adder #(.width(32)) adder_2 (.a(multiplier_3_out), .b(multiplier_4_out), .out(out_10));  // open: cin, cout
  Adder #(.width(32)) adder_3 (.a(multiplier_5_out), .b(multiplier_6_out), .out(out_11));  // open: cin, cout
  Adder #(.width(32)) adder_4 (.a(multiplier_7_out), .b(multiplier_8_out), .out(out_12));  // open: cin, cout
endmodule

module _1to32bit (
  input  in_1,
  output [31:0] out_2
);


  assign out_2 = {32{in_1}};
endmodule
