// Logisim project MUX.circ as structural Verilog
module _2_1_MUX (
  input  \第0位 ,
  input  \第1位 ,
  input  \地址选择 ,
  output out_4
);

  wire and_1_out, and_2_out, not_1_out;

  and and_1 (and_1_out, \第0位 , not_1_out);
  not not_1 (not_1_out, \地址选择 );
  and and_2 (and_2_out, \地址选择 , \第1位 );
  or or_1 (out_4, and_1_out, and_2_out);
endmodule

module _4_1_MUX (
  input  in_1,
  input  in_2,
  input  in_3,
  input  in_4,
  input  in_5,
  input  in_6,
  output out_7
);

  wire n2_1_mux_1_out_4, n2_1_mux_2_out_4;

  _2_1_MUX u_2_1_mux_1 (.\第1位 (in_2), .\第0位 (in_1), .out_4(n2_1_mux_1_out_4), .\地址选择 (in_6));
  _2_1_MUX u_2_1_mux_2 (.\第1位 (in_4), .\第0位 (in_3), .out_4(n2_1_mux_2_out_4), .\地址选择 (in_6));
  _2_1_MUX u_2_1_mux_3 (.\第1位 (n2_1_mux_2_out_4), .\第0位 (n2_1_mux_1_out_4), .out_4(out_7), .\地址选择 (in_5));
endmodule
