// Logisim project i周期输出2^i.circ as structural Verilog: 1 circuit, main circuit main
module main (
  input  [2:0] in_1,
  input  [7:0] in_2,
  input  in_3,
  input  in_4
);

  wire clock_1_out, comparator_1_lt;
  wire [7:0] N_1, Nth, shifter_1_out;

  // Probe on Nth
  // Probe on shifter_1_out
  Shifter shifter_1 (.in(Nth), .\dist (in_1), .out(shifter_1_out));
  // Probe on N_1
  Clock clock_1 (.out(clock_1_out));
  Register register_1 (.D(N_1), .en(in_3), .Q(Nth), .clk(clock_1_out), .clr(in_4));
  Comparator #(.mode("unsigned")) comparator_1 (.a(shifter_1_out), .b(in_2), .lt(comparator_1_lt));  // open: gt, eq
  // Probe on Nth
  Multiplexer #(.width(8), .enable("false")) multiplexer_1 (
    .in0(shifter_1_out), .in1(in_2), .out(N_1), .sel(comparator_1_lt));
  // Probe on N_1

  // Notes on the sheet:
  //   移位器
  //   Ctrl+K开始模拟
  //   16进制
  //   对输出进行移位后再输入
  //   避免移位到0后停止，和1作比较，取大的
endmodule
