// Logisim project mod5.circ as structural Verilog: 5 circuits, main circuit Logic
module Logic (
  input  I,
  input  S2,
  input  S1,
  input  S0,
  output NS2,
  output NS1,
  output NS0
);

  wire and_2_out, and_3_out, and_4_out, not_1_out, not_2_out, not_3_out, not_4_out;

  not not_1 (not_1_out, I);
  and and_1 (NS2, not_1_out, S1);
  not not_2 (not_2_out, I);
  and and_2 (and_2_out, not_2_out, not_3_out);
  not not_3 (not_3_out, S1);
  not not_4 (not_4_out, I);
  and and_3 (and_3_out, not_4_out, S2);
  and and_4 (and_4_out, I, S1);
  or or_1 (NS0, and_2_out, and_3_out, and_4_out);

  assign NS1 = I;
endmodule

module One_Hot_to_Nature (
  input  s4,
  input  s3,
  input  s2,
  input  s1,
  input  s0,
  output o3,
  output o2,
  output o1
);

  or or_1 (o2, s2, s3);
  or or_2 (o1, s1, s3);

  assign o3 = s4;
endmodule

module Nature_to_One_Hot (
  input  I3,
  input  I2,
  input  I1,
  output O4,
  output O3,
  output O2,
  output O1,
  output O0
);

  wire and_1_out, and_2_out, and_3_out, and_4_out, and_5_out, and_6_out, and_7_out, and_8_out, not_1_out,
       not_2_out, not_3_out, not_4_out, not_5_out, not_6_out, not_7_out, not_8_out, not_9_out;

  not not_1 (not_1_out, I2);
  not not_2 (not_2_out, I1);
  not not_3 (not_3_out, I3);
  not not_4 (not_4_out, I1);
  not not_5 (not_5_out, I3);
  not not_6 (not_6_out, I1);
  not not_7 (not_7_out, I3);
  not not_8 (not_8_out, I2);
  not not_9 (not_9_out, I1);
  and and_1 (and_1_out, I3, not_1_out, not_2_out);
  and and_2 (and_2_out, I3, I2, I1);
  and and_3 (and_3_out, not_3_out, I2, I1);
  and and_4 (and_4_out, I3, I2, not_4_out);
  and and_5 (and_5_out, not_5_out, I2, not_6_out);
  and and_6 (and_6_out, I3, I2, I1);
  and and_7 (and_7_out, not_7_out, not_8_out, I1);
  and and_8 (and_8_out, I3, I2, not_9_out);
  or or_1 (O4, and_1_out, and_2_out);
  or or_2 (O3, and_3_out, and_4_out);
  or or_3 (O2, and_5_out, and_6_out);
  or or_4 (O1, and_7_out, and_8_out);

  assign O0 = 1'b0;
endmodule

module mod5 (
  input  In,
  input  in_2,
  output out_3,
  output out_4,
  output out_5,
  output out_6,
  output out_7
);

  wire clock_1_out;
  wire [2:0] logic_1_ns0, out;

  Clock clock_1 (.out(clock_1_out));
  Logic logic_1 (
    .I(In), .S2(out[2]), .S1(out[1]), .S0(out[0]), .NS2(logic_1_ns0[2]), .NS1(logic_1_ns0[1]),
    .NS0(logic_1_ns0[0]));
  Nature_to_One_Hot nature_to_one_hot_1 (
    .I3(logic_1_ns0[2]), .I2(logic_1_ns0[1]), .I1(logic_1_ns0[0]), .O4(out_3), .O3(out_4), .O2(out_5),
    .O1(out_6), .O0(out_7));
  Register #(.width(3)) register_1 (.D(logic_1_ns0), .en(1'b1), .Q(out), .clk(clock_1_out), .clr(in_2));
endmodule

module test (
  input  in_1,
  output out_2,
  output out_3,
  output out_4,
  output out_5,
  output out_6
);

  wire clock_1_out, rom_1_data;
  wire [3:0] counter_1_q;

  Counter #(.width(4), .max('hf)) counter_1 (
    .Q(counter_1_q), .clk(clock_1_out), .clr(in_1));  // open: load, D, count, carry
  Clock clock_1 (.out(clock_1_out));
  ROM #(.addrWidth(4), .dataWidth(1)) rom_1 (.addr(counter_1_q), .data(rom_1_data));  // open: sel
  mod5 mod5_1 (
    .In(rom_1_data), .out_3(out_6), .out_4(out_5), .out_5(out_4), .out_6(out_3), .out_7(out_2));  // open: in_2

  // Notes on the sheet:
  //   contents of rom_1 (hex, n*v repeats v):
  //   0 1 0 0 1 0 0 1 0 0 1 0 0 1
endmodule
