// Logisim project 循环移位.circ as structural Verilog: 8 circuits, main circuit main
module main (
  input  [7:0] in_1,
  input  [2:0] in_2,
  output [7:0] out_3
);

  wire [7:0] shift1_1_out_2, shift2_1_out_2, shift3_1_out_2, shift4_1_out_2, shift5_1_out_2, shift6_1_out_2,
       shift7_1_out_2;

  shift1 shift1_1 (.in_1(in_1), .out_2(shift1_1_out_2));
  shift2 shift2_1 (.in_1(in_1), .out_2(shift2_1_out_2));
  shift3 shift3_1 (.in_1(in_1), .out_2(shift3_1_out_2));
  shift4 shift4_1 (.in_1(in_1), .out_2(shift4_1_out_2));
  shift5 shift5_1 (.in_1(in_1), .out_2(shift5_1_out_2));
  shift6 shift6_1 (.in_1(in_1), .out_2(shift6_1_out_2));
  shift7 shift7_1 (.in_1(in_1), .out_2(shift7_1_out_2));
  Multiplexer #(.select(3), .width(8)) multiplexer_1 (
    .in0(in_1), .in1(shift1_1_out_2), .in2(shift2_1_out_2), .in3(shift3_1_out_2), .in4(shift4_1_out_2),
    .in5(shift5_1_out_2), .in6(shift6_1_out_2), .in7(shift7_1_out_2), .out(out_3), .sel(in_2));  // open: en

  // Notes on the sheet:
  //   8位循环左移移位器
endmodule

module shift1 (
  input  [7:0] in_1,
  output [7:0] out_2
);


  assign out_2 = {in_1[6:0], in_1[7]};
endmodule

module shift2 (
  input  [7:0] in_1,
  output [7:0] out_2
);


  assign out_2 = {in_1[5:0], in_1[7:6]};
endmodule

module shift3 (
  input  [7:0] in_1,
  output [7:0] out_2
);


  assign out_2 = {in_1[4:0], in_1[7:5]};
endmodule

module shift4 (
  input  [7:0] in_1,
  output [7:0] out_2
);


  assign out_2 = {in_1[3:0], in_1[7:4]};
endmodule

module shift5 (
  input  [7:0] in_1,
  output [7:0] out_2
);


  assign out_2 = {in_1[2:0], in_1[7:3]};
endmodule

module shift6 (
  input  [7:0] in_1,
  output [7:0] out_2
);


  assign out_2 = {in_1[1:0], in_1[7:2]};
endmodule

module shift7 (
  input  [7:0] in_1,
  output [7:0] out_2
);


  assign out_2 = {in_1[0], in_1[7:1]};
endmodule
