// Logisim project 排序电路.circ as structural Verilog: 3 circuits, main circuit 1bit_swap
module _1bit_swap (
  input  I1,
  input  I2,
  input  S,
  output O1,
  output O2
);

  wire and_1_out, and_2_out, and_3_out, and_4_out, not_1_out, not_2_out;

  not not_1 (not_1_out, S);
  not not_2 (not_2_out, S);
  and and_1 (and_1_out, not_1_out, I1);
  and and_2 (and_2_out, S, I2);
  and and_3 (and_3_out, not_2_out, I2);
  and and_4 (and_4_out, S, I1);
  or or_1 (O1, and_1_out, and_1_out, and_2_out, and_2_out);
  or or_2 (O2, and_3_out, and_3_out, and_4_out, and_4_out);
endmodule

module _4bit_swap (
  input  [3:0] I1,
  input  [3:0] I2,
  input  S,
  output [3:0] O1,
  output [3:0] O2
);

  _1bit_swap u_1bit_swap_1 (.S(S), .I1(I1[0]), .I2(I2[0]), .O1(O1[0]), .O2(O2[0]));
  _1bit_swap u_1bit_swap_2 (.S(S), .I1(I1[1]), .I2(I2[1]), .O1(O1[1]), .O2(O2[1]));
  _1bit_swap u_1bit_swap_3 (.S(S), .I1(I1[2]), .I2(I2[2]), .O1(O1[2]), .O2(O2[2]));
  _1bit_swap u_1bit_swap_4 (.S(S), .I1(I1[3]), .I2(I2[3]), .O1(O1[3]), .O2(O2[3]));

  // Other names for the same wires on the sheet: x0 = I1[0]; x1 = I1[1]; x2 = I1[2]; x3 = I1[3]; y0 = I2[0];
  //   y1 = I2[1]; y2 = I2[2]; y3 = I2[3]
endmodule

module _4bit_sort (
  input  [3:0] in_1,
  input  [3:0] in_2,
  input  [3:0] in_3,
  input  [3:0] in_4,
  output [3:0] O1,
  output [3:0] O2,
  output [3:0] O3,
  output [3:0] O4
);

  wire comparator_1_lt, comparator_2_lt, comparator_3_lt, comparator_4_lt, comparator_5_lt;
  wire [3:0] n4bit_swap_1_o1, n4bit_swap_1_o2, n4bit_swap_2_o1, n4bit_swap_2_o2, n4bit_swap_3_o2,
       n4bit_swap_4_o1;

  Comparator #(.width(4), .mode("unsigned")) comparator_1 (.a(in_1), .b(in_2), .lt(comparator_1_lt));  // open: gt, eq
  Comparator #(.width(4), .mode("unsigned")) comparator_2 (.a(in_3), .b(in_4), .lt(comparator_2_lt));  // open: gt, eq
  // Probe on n4bit_swap_1_o1
  // Probe on n4bit_swap_2_o1
  _4bit_swap u_4bit_swap_1 (.I1(in_1), .I2(in_2), .S(comparator_1_lt), .O1(n4bit_swap_1_o1), .O2(n4bit_swap_1_o2));
  _4bit_swap u_4bit_swap_2 (.I1(in_3), .I2(in_4), .S(comparator_2_lt), .O1(n4bit_swap_2_o1), .O2(n4bit_swap_2_o2));
  _4bit_swap u_4bit_swap_3 (
    .I1(n4bit_swap_1_o1), .I2(n4bit_swap_2_o1), .S(comparator_3_lt), .O1(O1), .O2(n4bit_swap_3_o2));
  Comparator #(.width(4), .mode("unsigned")) comparator_3 (
    .a(n4bit_swap_1_o1), .b(n4bit_swap_2_o1), .lt(comparator_3_lt));  // open: gt, eq
  // Probe on n4bit_swap_2_o2
  // Probe on n4bit_swap_1_o2
  _4bit_swap u_4bit_swap_4 (
    .I1(n4bit_swap_2_o2), .I2(n4bit_swap_1_o2), .S(comparator_4_lt), .O1(n4bit_swap_4_o1), .O2(O4));
  Comparator #(.width(4), .mode("unsigned")) comparator_4 (
    .a(n4bit_swap_2_o2), .b(n4bit_swap_1_o2), .lt(comparator_4_lt));  // open: gt, eq
  // Probe on n4bit_swap_3_o2
  // Probe on n4bit_swap_4_o1
  _4bit_swap u_4bit_swap_5 (.I1(n4bit_swap_3_o2), .I2(n4bit_swap_4_o1), .S(comparator_5_lt), .O1(O2), .O2(O3));
  Comparator #(.width(4), .mode("unsigned")) comparator_5 (
    .a(n4bit_swap_3_o2), .b(n4bit_swap_4_o1), .lt(comparator_5_lt));  // open: gt, eq

  // Other names for the same wires on the sheet: A[3:0] = in_1; B[3:0] = in_2; C[3:0] = in_3; D[3:0] = in_4
endmodule
