// Logisim project ftoi（附加题）.circ as structural Verilog: 5 circuits, main circuit ftoi
module ftoi (
  input  [15:0] float,
  output [31:0] \int 
);

  wire comparator_2_eq, comparator_3_eq, is_neg;
  wire [1:0] which;
  wire [31:0] adder_1_out, multiplexer_1_out, norm_1_int;

  Norm norm_1 (.in_1(float), .\int (norm_1_int));
  Multiplexer #(.select(2), .width(32), .enable("false")) multiplexer_1 (
    .in0(norm_1_int), .in1({32{1'b0}}), .in2({32{1'b0}}), .out(multiplexer_1_out), .sel(which));  // open: in3
  Adder #(.width(32)) adder_1 (.a(32'h1), .b(multiplexer_1_out), .out(adder_1_out));  // open: cin, cout
  Comparator #(.width(32)) comparator_1 (.a(multiplexer_1_out), .b({32{1'b0}}), .lt(is_neg));  // open: gt, eq
  Comparator #(.width(5), .mode("unsigned")) comparator_2 (
    .a({5{1'b0}}), .b(float[14:10]), .eq(comparator_2_eq));  // open: gt, lt
  which_type which_type_1 (.IfNa(comparator_3_eq), .Denom(comparator_2_eq), .type1(which[1]), .type0(which[0]));
  Comparator #(.width(5), .mode("unsigned")) comparator_3 (
    .a({5{1'b1}}), .b(float[14:10]), .eq(comparator_3_eq));  // open: gt, lt
  Multiplexer #(.width(32), .enable("false")) multiplexer_2 (
    .in0(multiplexer_1_out), .in1(adder_1_out), .out(\int ), .sel(is_neg));
  // Probe on which
  // Probe on \int 

  // Notes on the sheet:
  //   除了Norm，输出都是0
  //   is denorm?
  //   is Infity/NaN?
  //   是负数要加一
endmodule

module which_type (
  input  IfNa,
  input  Denom,
  output type1,
  output type0
);

  wire not_1_out, not_2_out;

  not not_1 (not_1_out, Denom);
  not not_2 (not_2_out, IfNa);
  and and_1 (type1, IfNa, not_1_out);
  and and_2 (type0, not_2_out, Denom);
endmodule

module \乘还是除以n的x次方  (
  input  [4:0] exp,
  output [4:0] n,
  output \乘还是除 
);

  wire [4:0] diff;

  Subtractor #(.width(5)) subtractor_1 (.a(exp), .b(5'b01111), .out(diff), .bout(\乘还是除 ));  // open: bin
  Multiplexer #(.width(5), .enable("false")) multiplexer_1 (.in0(diff), .in1({5{1'b0}}), .out(n), .sel(\乘还是除 ));
  // Probe on n

  // Notes on the sheet:
  //   乘还是除以2的n次方
  //   除以的话，直接输出0
endmodule

module Norm (
  input  [15:0] in_1,
  output [31:0] \int 
);

  wire \乘还是除 ;
  wire [4:0] n;
  wire [31:0] _2_n, adder_2_out, adder_3_out, adder_4_out, adder_5_out, adder_6_out, adder_7_out,
       adder_8_out, adder_9_out, divider_1_out, divider_2_out, divider_3_out, divider_4_out, divider_5_out,
       divider_6_out, divider_7_out, divider_8_out, divider_9_out, divider_10_out, \final , frac,
       multiplexer_1_out, multiplexer_2_out, multiplexer_3_out, multiplexer_4_out, multiplexer_5_out,
       multiplexer_6_out, multiplexer_7_out, multiplexer_8_out, multiplexer_9_out, multiplexer_10_out,
       \output , subtractor_1_out;

  \乘还是除以n的x次方  \u_乘还是除以n的x次方_1  (.exp(in_1[14:10]), .n(n), .\乘还是除 (\乘还是除 ));
  _2_n u_2_n_1 (.in_1(n), .out_2(_2_n));
  Adder #(.width(32)) adder_1 (.a(frac), .b(_2_n), .out(\output ));  // open: cin, cout
  Divider #(.width(32)) divider_1 (.a(_2_n), .b(32'h400), .out(divider_1_out));  // open: upper, rem
  Divider #(.width(32)) divider_2 (.a(_2_n), .b(32'h200), .out(divider_2_out));  // open: upper, rem
  Divider #(.width(32)) divider_3 (.a(_2_n), .b(32'h100), .out(divider_3_out));  // open: upper, rem
  Divider #(.width(32)) divider_4 (.a(_2_n), .b(32'h80), .out(divider_4_out));  // open: upper, rem
  Divider #(.width(32)) divider_5 (.a(_2_n), .b(32'h40), .out(divider_5_out));  // open: upper, rem
  Divider #(.width(32)) divider_6 (.a(_2_n), .b(32'h20), .out(divider_6_out));  // open: upper, rem
  Divider #(.width(32)) divider_7 (.a(_2_n), .b(32'h10), .out(divider_7_out));  // open: upper, rem
  Divider #(.width(32)) divider_8 (.a(_2_n), .b(32'h8), .out(divider_8_out));  // open: upper, rem
  Divider #(.width(32)) divider_9 (.a(_2_n), .b(32'h4), .out(divider_9_out));  // open: upper, rem
  Divider #(.width(32)) divider_10 (.a(_2_n), .b(32'h2), .out(divider_10_out));  // open: upper, rem
  Multiplexer #(.width(32), .enable("false")) multiplexer_1 (
    .in0({32{1'b0}}), .in1(divider_1_out), .out(multiplexer_1_out), .sel(in_1[0]));
  Multiplexer #(.width(32), .enable("false")) multiplexer_2 (
    .in0({32{1'b0}}), .in1(divider_2_out), .out(multiplexer_2_out), .sel(in_1[1]));
  Multiplexer #(.width(32), .enable("false")) multiplexer_3 (
    .in0({32{1'b0}}), .in1(divider_3_out), .out(multiplexer_3_out), .sel(in_1[2]));
  Multiplexer #(.width(32), .enable("false")) multiplexer_4 (
    .in0({32{1'b0}}), .in1(divider_4_out), .out(multiplexer_4_out), .sel(in_1[3]));
  Multiplexer #(.width(32), .enable("false")) multiplexer_5 (
    .in0({32{1'b0}}), .in1(divider_5_out), .out(multiplexer_5_out), .sel(in_1[4]));
  Multiplexer #(.width(32), .enable("false")) multiplexer_6 (
    .in0({32{1'b0}}), .in1(divider_6_out), .out(multiplexer_6_out), .sel(in_1[5]));
  Multiplexer #(.width(32), .enable("false")) multiplexer_7 (
    .in0({32{1'b0}}), .in1(divider_7_out), .out(multiplexer_7_out), .sel(in_1[6]));
  Multiplexer #(.width(32), .enable("false")) multiplexer_8 (
    .in0({32{1'b0}}), .in1(divider_8_out), .out(multiplexer_8_out), .sel(in_1[7]));
  Multiplexer #(.width(32), .enable("false")) multiplexer_9 (
    .in0({32{1'b0}}), .in1(divider_9_out), .out(multiplexer_9_out), .sel(in_1[8]));
  Multiplexer #(.width(32), .enable("false")) multiplexer_10 (
    .in0({32{1'b0}}), .in1(divider_10_out), .out(multiplexer_10_out), .sel(in_1[9]));
  Subtractor #(.width(32)) subtractor_1 (.a({32{1'b1}}), .b(\output ), .out(subtractor_1_out));  // open: bin, bout
  Adder #(.width(32)) adder_2 (.a(multiplexer_1_out), .b(multiplexer_2_out), .out(adder_2_out));  // open: cin, cout
  Adder #(.width(32)) adder_3 (.a(multiplexer_3_out), .b(multiplexer_4_out), .out(adder_3_out));  // open: cin, cout
  Adder #(.width(32)) adder_4 (.a(multiplexer_5_out), .b(multiplexer_6_out), .out(adder_4_out));  // open: cin, cout
  Adder #(.width(32)) adder_5 (.a(multiplexer_7_out), .b(multiplexer_8_out), .out(adder_5_out));  // open: cin, cout
  Adder #(.width(32)) adder_6 (.a(multiplexer_9_out), .b(multiplexer_10_out), .out(adder_6_out));  // open: cin, cout
  Multiplexer #(.width(32), .enable("false")) multiplexer_11 (
    .in0(\output ), .in1(subtractor_1_out), .out(\final ), .sel(in_1[15]));
  Adder #(.width(32)) adder_7 (.a(adder_2_out), .b(adder_3_out), .out(adder_7_out));  // open: cin, cout
  Adder #(.width(32)) adder_8 (.a(adder_4_out), .b(adder_5_out), .out(adder_8_out));  // open: cin, cout
  Adder #(.width(32)) adder_9 (.a(adder_7_out), .b(adder_8_out), .out(adder_9_out));  // open: cin, cout
  Multiplexer #(.width(32), .enable("false")) multiplexer_12 (
    .in0(\final ), .in1({32{1'b0}}), .out(\int ), .sel(\乘还是除 ));
  // Probe on \int 
  Adder #(.width(32)) adder_10 (.a(adder_9_out), .b(adder_6_out), .out(frac));  // open: cin, cout
  // Probe on frac

  // Other names for the same wires on the sheet: input[15:0] = in_1; 除以_2_10 = in_1[0]; 除以_2_9 = in_1[1];
  //   除以_2_8 = in_1[2]; 除以_2_7 = in_1[3]; 除以_2_6 = in_1[4]; 除以_2_5 = in_1[5]; 除以_2_4 = in_1[6]; 除以_2_3 = in_1[7];
  //   除以_2_2 = in_1[8]; 除以_2_1 = in_1[9]; sign = in_1[15]

  // Notes on the sheet:
  //   2^n和frac的每一位相乘，然后因为前导1，还要加上自身，得到output
  //   判断是不是负数
  //   是负数的话，还要取相反数
endmodule

module _2_n (
  input  [4:0] in_1,
  output [31:0] out_2
);

  wire [31:0] multiplexer_1_out, multiplexer_2_out, multiplexer_3_out, multiplexer_4_out, multiplexer_5_out,
       multiplier_1_out, multiplier_2_out, multiplier_3_out;

  // Probe on 32'h10000
  // Probe on in_1
  Multiplexer #(.width(32), .enable("false")) multiplexer_1 (
    .in0(32'h1), .in1(32'h2), .out(multiplexer_1_out), .sel(in_1[0]));
  Multiplexer #(.width(32), .enable("false")) multiplexer_2 (
    .in0(32'h1), .in1(32'h4), .out(multiplexer_2_out), .sel(in_1[1]));
  Multiplexer #(.width(32), .enable("false")) multiplexer_3 (
    .in0(32'h1), .in1(32'h10), .out(multiplexer_3_out), .sel(in_1[2]));
  Multiplexer #(.width(32), .enable("false")) multiplexer_4 (
    .in0(32'h1), .in1(32'h100), .out(multiplexer_4_out), .sel(in_1[3]));
  Multiplexer #(.width(32), .enable("false")) multiplexer_5 (
    .in0(32'h1), .in1(32'h10000), .out(multiplexer_5_out), .sel(in_1[4]));
  Multiplier #(.width(32)) multiplier_1 (
    .a(multiplexer_1_out), .b(multiplexer_2_out), .out(multiplier_1_out));  // open: cin, cout
  Multiplier #(.width(32)) multiplier_2 (
    .a(multiplexer_3_out), .b(multiplexer_4_out), .out(multiplier_2_out));  // open: cin, cout
  Multiplier #(.width(32)) multiplier_3 (
    .a(multiplier_2_out), .b(multiplexer_5_out), .out(multiplier_3_out));  // open: cin, cout
  Multiplier #(.width(32)) multiplier_4 (.a(multiplier_1_out), .b(multiplier_3_out), .out(out_2));  // open: cin, cout
  // Probe on out_2

  // Other names for the same wires on the sheet: _2_1 = in_1[0]; _2_2 = in_1[1]; _2_4 = in_1[2]; _2_8 = in_1[3];
  //   _2_16 = in_1[4]

  // Notes on the sheet:
  //   给定2进制数n，输出其n次方
endmodule
