// Logisim project 1-CRC校验.circ as structural Verilog: 2 circuits, main circuit CRC
module CRC (
  input  [7:0] \被除数 ,
  input  [3:0] \除数 ,
  output [10:0] out_3
);

  wire [2:0] n4digits_mod2_1_out_4, n4digits_mod2_2_out_4, n4digits_mod2_3_out_4, n4digits_mod2_4_out_4,
       n4digits_mod2_5_out_4, n4digits_mod2_6_out_4, n4digits_mod2_7_out_4;

  _4digits_mod2 u_4digits_mod2_1 (.\被除数 (\被除数 [7:4]), .\除数 (\除数 ), .out_4(n4digits_mod2_1_out_4));  // open: out_3
  _4digits_mod2 u_4digits_mod2_2 (
    .\被除数 ({n4digits_mod2_1_out_4, \被除数 [3]}), .\除数 (\除数 ), .out_4(n4digits_mod2_2_out_4));  // open: out_3
  _4digits_mod2 u_4digits_mod2_3 (
    .\被除数 ({n4digits_mod2_2_out_4, \被除数 [2]}), .\除数 (\除数 ), .out_4(n4digits_mod2_3_out_4));  // open: out_3
  _4digits_mod2 u_4digits_mod2_4 (
    .\被除数 ({n4digits_mod2_3_out_4, \被除数 [1]}), .\除数 (\除数 ), .out_4(n4digits_mod2_4_out_4));  // open: out_3
  _4digits_mod2 u_4digits_mod2_5 (
    .\被除数 ({n4digits_mod2_4_out_4, \被除数 [0]}), .\除数 (\除数 ), .out_4(n4digits_mod2_5_out_4));  // open: out_3
  _4digits_mod2 u_4digits_mod2_6 (
    .\被除数 ({n4digits_mod2_5_out_4, 1'b0}), .\除数 (\除数 ), .out_4(n4digits_mod2_6_out_4));  // open: out_3
  _4digits_mod2 u_4digits_mod2_7 (
    .\被除数 ({n4digits_mod2_6_out_4, 1'b0}), .\除数 (\除数 ), .out_4(n4digits_mod2_7_out_4));  // open: out_3
  _4digits_mod2 u_4digits_mod2_8 (
    .\被除数 ({n4digits_mod2_7_out_4, 1'b0}), .\除数 (\除数 ), .out_4(out_3[2:0]));  // open: out_3

  assign out_3[10:3] = \被除数 ;

  // Other names for the same wires on the sheet: A[7:0] = \被除数 ; A2 = \被除数 [2]; A1 = \被除数 [1]; A0 = \被除数 [0];
  //   B[3:0] = \除数 ; 余数[2:0] = out_3[2:0]; A3 = \被除数 [3]; A4 = \被除数 [4]; A5 = \被除数 [5]; A6 = \被除数 [6]; A7 = \被除数 [7]
endmodule

module _4digits_mod2 (
  input  [3:0] \被除数 ,
  input  [3:0] \除数 ,
  output out_3,
  output [2:0] out_4
);

  wire [3:0] xor_1_out;
  wire [3:3] multiplexer_1_out;

  // Probe on \被除数 
  assign xor_1_out = \被除数  ^ \除数 ;  // XOR_Gate xor_1, 4 bits wide
  // Probe on xor_1_out
  Multiplexer #(.width(4)) multiplexer_1 (
    .in0(\被除数 ), .in1(xor_1_out), .out({multiplexer_1_out[3], out_4}), .sel(\被除数 [3]));  // open: en

  assign out_3 = \被除数 [3];

  // Other names for the same wires on the sheet: 最高位 = \被除数 [3]
endmodule
