// Logisim project 3-Logisim导航.circ as structural Verilog: 3 circuits, main circuit navigation
module navigation (
  input  [1:0] dir,
  input  clk,
  input  reset,
  output arrive,
  output hit
);

  wire hit_logic_1_x;
  wire [2:0] current_state, state_transfer_ns0;

  Comparator #(.width(3), .mode("unsigned")) comparator_1 (.a(current_state), .b(3'b100), .eq(arrive));  // open: gt, lt
  hit_logic hit_logic_1 (
    .s2(current_state[2]), .s1(current_state[1]), .s0(current_state[0]), .dir1(dir[1]), .dir0(dir[0]),
    .x(hit_logic_1_x));
  state_transfer state_transfer (
    .s2(current_state[2]), .s1(current_state[1]), .s0(current_state[0]), .dir1(dir[1]), .dir0(dir[0]),
    .Ns2(state_transfer_ns0[2]), .Ns1(state_transfer_ns0[1]), .Ns0(state_transfer_ns0[0]));
  Register #(.width(1)) u_hit (.D(hit_logic_1_x), .Q(hit), .clk(clk), .clr(reset));  // open: en
  Register #(.width(3)) state (.D(state_transfer_ns0), .Q(current_state), .clk(clk), .clr(reset));  // open: en

  // Notes on the sheet:
  //   hit logic
endmodule

module hit_logic (
  input  s2,
  input  s1,
  input  s0,
  input  dir1,
  input  dir0,
  output x
);

  wire and_1_out, and_2_out, and_3_out, and_4_out, and_5_out, and_6_out, not_1_out, not_2_out, not_3_out,
       not_4_out, not_5_out, not_6_out, not_7_out, not_8_out, not_9_out, not_10_out, not_11_out;

  not not_1 (not_1_out, s2);
  not not_2 (not_2_out, s0);
  not not_3 (not_3_out, dir1);
  not not_4 (not_4_out, s2);
  not not_5 (not_5_out, s1);
  not not_6 (not_6_out, s0);
  not not_7 (not_7_out, s2);
  not not_8 (not_8_out, s0);
  not not_9 (not_9_out, dir0);
  not not_10 (not_10_out, dir1);
  not not_11 (not_11_out, dir0);
  and and_1 (and_1_out, not_1_out, not_2_out, not_3_out, dir0);
  and and_2 (and_2_out, not_4_out, not_5_out, not_6_out, dir1);
  and and_3 (and_3_out, not_7_out, not_8_out, dir1, not_9_out);
  and and_4 (and_4_out, s0, dir1, dir0);
  and and_5 (and_5_out, s1, s0, not_10_out, not_11_out);
  and and_6 (and_6_out, s2, s0);
  or or_1 (x, and_1_out, and_2_out, and_3_out, and_4_out, and_5_out, and_6_out);
endmodule

module state_transfer (
  input  s2,
  input  s1,
  input  s0,
  input  dir1,
  input  dir0,
  output Ns2,
  output Ns1,
  output Ns0
);

  wire and_1_out, and_2_out, and_3_out, and_4_out, and_5_out, and_6_out, and_7_out, and_8_out, and_9_out,
       and_10_out, and_11_out, not_1_out, not_2_out, not_3_out, not_4_out, not_5_out, not_6_out, not_7_out,
       not_8_out, not_9_out, not_10_out, not_11_out, not_12_out, not_13_out, not_14_out, not_15_out,
       not_16_out, not_17_out;

  not not_1 (not_1_out, s0);
  not not_2 (not_2_out, dir1);
  not not_3 (not_3_out, dir0);
  not not_4 (not_4_out, dir1);
  not not_5 (not_5_out, s1);
  not not_6 (not_6_out, dir1);
  not not_7 (not_7_out, dir1);
  not not_8 (not_8_out, dir0);
  not not_9 (not_9_out, s0);
  not not_10 (not_10_out, dir1);
  not not_11 (not_11_out, s0);
  not not_12 (not_12_out, dir0);
  not not_13 (not_13_out, s2);
  not not_14 (not_14_out, s1);
  not not_15 (not_15_out, dir1);
  not not_16 (not_16_out, dir0);
  not not_17 (not_17_out, dir0);
  and and_1 (and_1_out, s1, not_1_out, not_2_out, not_3_out);
  and and_2 (and_2_out, s1, s0, not_4_out, dir0);
  and and_3 (and_3_out, not_5_out, s0, not_6_out);
  and and_4 (and_4_out, s0, not_7_out, not_8_out);
  and and_5 (and_5_out, s1, not_9_out, not_10_out, dir0);
  and and_6 (and_6_out, s1, not_11_out, dir1, not_12_out);
  and and_7 (and_7_out, s1, s0, dir1, dir0);
  and and_8 (and_8_out, not_13_out, not_14_out, not_15_out, not_16_out);
  and and_9 (and_9_out, s0, dir1, dir0);
  and and_10 (and_10_out, s1, dir1, dir0);
  and and_11 (and_11_out, s1, s0, not_17_out);
  or or_1 (Ns2, and_1_out, and_2_out);
  or or_2 (Ns1, and_3_out, and_4_out, and_5_out, and_6_out, and_7_out);
  or or_3 (Ns0, and_8_out, and_9_out, and_10_out, and_11_out);
endmodule
