// Logisim project 售货机1.circ as structural Verilog: 3 circuits, main circuit main
module main (
  input  [1:0] In,
  output dispense,
  output [2:0] change
);

  wire clock_1_out, comparator_1_eq, comparator_1_gt;
  wire [3:0] cur_state, state_trans_1_ns0;

  Comparator #(.width(4), .mode("unsigned")) comparator_1 (
    .a(cur_state), .b(4'b0101), .gt(comparator_1_gt), .eq(comparator_1_eq));  // open: lt
  state_trans state_trans_1 (
    .s3(cur_state[3]), .s2(cur_state[2]), .s1(cur_state[1]), .s0(cur_state[0]), .In1(In[1]), .In0(In[0]),
    .Ns3(state_trans_1_ns0[3]), .Ns2(state_trans_1_ns0[2]), .Ns1(state_trans_1_ns0[1]),
    .Ns0(state_trans_1_ns0[0]));
  change change_1 (
    .s3(cur_state[3]), .s2(cur_state[2]), .s1(cur_state[1]), .s0(cur_state[0]), .change2(change[2]),
    .change1(change[1]), .change0(change[0]));
  // Probe on change
  or or_1 (dispense, comparator_1_gt, comparator_1_eq);
  Register #(.width(4)) register_1 (.D(state_trans_1_ns0), .Q(cur_state), .clk(clock_1_out));  // open: en, clr
  // Probe on cur_state
  Clock clock_1 (.out(clock_1_out));
endmodule

module state_trans (
  input  s3,
  input  s2,
  input  s1,
  input  s0,
  input  In1,
  input  In0,
  output Ns3,
  output Ns2,
  output Ns1,
  output Ns0
);

  wire and_1_out, and_2_out, and_3_out, and_4_out, and_5_out, and_6_out, and_7_out, and_8_out, and_9_out,
       and_10_out, and_11_out, and_12_out, and_13_out, and_14_out, and_15_out, and_16_out, not_1_out,
       not_2_out, not_3_out, not_4_out, not_5_out, not_6_out, not_7_out, not_8_out, not_9_out, not_10_out,
       not_11_out, not_12_out, not_13_out, not_14_out, not_15_out, not_16_out, not_17_out, not_18_out,
       not_19_out, not_20_out, not_21_out, not_22_out, not_23_out, not_24_out, not_25_out, not_26_out,
       not_27_out, not_28_out, not_29_out, not_30_out, not_31_out, not_32_out, not_33_out, not_34_out,
       not_35_out, not_36_out, not_37_out, not_38_out, not_39_out, not_40_out, not_41_out, not_42_out,
       not_43_out;

  not not_1 (not_1_out, s2);
  not not_2 (not_2_out, s1);
  not not_3 (not_3_out, s0);
  not not_4 (not_4_out, s3);
  not not_5 (not_5_out, s2);
  not not_6 (not_6_out, s1);
  not not_7 (not_7_out, s2);
  not not_8 (not_8_out, s0);
  not not_9 (not_9_out, s2);
  not not_10 (not_10_out, In0);
  not not_11 (not_11_out, s2);
  not not_12 (not_12_out, In1);
  not not_13 (not_13_out, s1);
  not not_14 (not_14_out, s0);
  not not_15 (not_15_out, In1);
  not not_16 (not_16_out, s1);
  not not_17 (not_17_out, s0);
  not not_18 (not_18_out, In0);
  not not_19 (not_19_out, s3);
  not not_20 (not_20_out, s2);
  not not_21 (not_21_out, s1);
  not not_22 (not_22_out, In0);
  not not_23 (not_23_out, s3);
  not not_24 (not_24_out, s1);
  not not_25 (not_25_out, s0);
  not not_26 (not_26_out, In0);
  not not_27 (not_27_out, s3);
  not not_28 (not_28_out, s2);
  not not_29 (not_29_out, s1);
  not not_30 (not_30_out, s2);
  not not_31 (not_31_out, In1);
  not not_32 (not_32_out, In0);
  not not_33 (not_33_out, s2);
  not not_34 (not_34_out, s0);
  not not_35 (not_35_out, s3);
  not not_36 (not_36_out, s2);
  not not_37 (not_37_out, s0);
  not not_38 (not_38_out, s3);
  not not_39 (not_39_out, s1);
  not not_40 (not_40_out, s0);
  not not_41 (not_41_out, s3);
  not not_42 (not_42_out, s2);
  not not_43 (not_43_out, In0);
  and and_1 (and_1_out, not_1_out, s1, s0, In1, In0);
  or or_1 (Ns3, and_1_out, and_2_out);
  and and_2 (and_2_out, s2, not_2_out, not_3_out, In1, In0);
  and and_3 (and_3_out, not_4_out, not_5_out, not_6_out, In1, In0);
  and and_4 (and_4_out, not_7_out, s1, not_8_out, In1);
  and and_5 (and_5_out, not_9_out, s1, In1, not_10_out);
  and and_6 (and_6_out, not_11_out, s1, s0, not_12_out, In0);
  and and_7 (and_7_out, s2, not_13_out, not_14_out, not_15_out);
  and and_8 (and_8_out, s2, not_16_out, not_17_out, not_18_out);
  and and_9 (and_9_out, not_19_out, not_20_out, not_21_out, In1, not_22_out);
  and and_10 (and_10_out, not_23_out, not_24_out, not_25_out, In1, not_26_out);
  and and_11 (and_11_out, not_27_out, not_28_out, not_29_out, s0, In0);
  and and_12 (and_12_out, not_30_out, s1, not_31_out, not_32_out);
  and and_13 (and_13_out, not_33_out, s1, not_34_out, In0);
  and and_14 (and_14_out, not_35_out, not_36_out, not_37_out, In0);
  and and_15 (and_15_out, not_38_out, not_39_out, not_40_out, In0);
  or or_2 (Ns0, and_14_out, and_15_out, and_16_out);
  and and_16 (and_16_out, not_41_out, not_42_out, s0, not_43_out);
  or or_3 (Ns2, and_3_out, and_4_out, and_5_out, and_6_out, and_7_out, and_8_out);
  or or_4 (Ns1, and_9_out, and_10_out, and_11_out, and_12_out, and_13_out);
endmodule

module change (
  input  s3,
  input  s2,
  input  s1,
  input  s0,
  output change2,
  output change1,
  output change0
);

  wire and_2_out, and_3_out, and_4_out, and_5_out, not_1_out, not_2_out, not_3_out;

  and and_1 (change2, s3, s0);
  not not_1 (not_1_out, s0);
  not not_2 (not_2_out, s0);
  not not_3 (not_3_out, s0);
  and and_2 (and_2_out, s2, s1, s0);
  and and_3 (and_3_out, s3, not_1_out);
  and and_4 (and_4_out, s2, s1, not_2_out);
  and and_5 (and_5_out, s3, not_3_out);
  or or_1 (change1, and_2_out, and_3_out);
  or or_2 (change0, and_4_out, and_5_out);
endmodule
