// Logisim project 售货机2.circ as structural Verilog: 3 circuits, main circuit main
module main (
  input  [1:0] In,
  output dis,
  output [2:0] change
);

  wire clk, comparator_1_lt;
  wire [2:0] change_1_change0, cur_state, state_trans_1_ns0;

  // Probe on nothing
  Clock clock_1 (.out(clk));
  state_trans state_trans_1 (
    .s2(cur_state[2]), .s1(cur_state[1]), .s0(cur_state[0]), .In1(In[1]), .In0(In[0]),
    .Ns2(state_trans_1_ns0[2]), .Ns1(state_trans_1_ns0[1]), .Ns0(state_trans_1_ns0[0]));
  change change_1 (
    .s2(cur_state[2]), .s1(cur_state[1]), .s0(cur_state[0]), .In1(In[1]), .In0(In[0]),
    .change2(change_1_change0[2]), .change1(change_1_change0[1]), .change0(change_1_change0[0]));
  Comparator #(.width(3), .mode("unsigned")) comparator_1 (
    .a(cur_state), .b(3'b101), .lt(comparator_1_lt));  // open: gt, eq
  not not_1 (dis, comparator_1_lt);
  // Probe on state_trans_1_ns0
  Register #(.width(3)) register_1 (.D(change_1_change0), .Q(change), .clk(clk));  // open: en, clr
  // Probe on nothing
  Register #(.width(3)) register_2 (.D(state_trans_1_ns0), .Q(cur_state), .clk(clk));  // open: en, clr
  // Probe on cur_state
  // Probe on change
endmodule

module state_trans (
  input  s2,
  input  s1,
  input  s0,
  input  In1,
  input  In0,
  output Ns2,
  output Ns1,
  output Ns0
);

  wire and_1_out, and_2_out, and_3_out, and_4_out, and_5_out, and_6_out, and_7_out, and_8_out, and_9_out,
       and_10_out, and_11_out, and_12_out, not_1_out, not_2_out, not_3_out, not_4_out, not_5_out, not_6_out,
       not_7_out, not_8_out, not_9_out, not_10_out, not_11_out, not_12_out, not_13_out, not_14_out,
       not_15_out, not_16_out, not_17_out, not_18_out, not_19_out, not_20_out;

  not not_1 (not_1_out, s2);
  not not_2 (not_2_out, s1);
  not not_3 (not_3_out, s0);
  not not_4 (not_4_out, s2);
  not not_5 (not_5_out, s1);
  not not_6 (not_6_out, In0);
  not not_7 (not_7_out, s2);
  not not_8 (not_8_out, s1);
  not not_9 (not_9_out, In1);
  not not_10 (not_10_out, s2);
  not not_11 (not_11_out, s0);
  not not_12 (not_12_out, In1);
  not not_13 (not_13_out, s2);
  not not_14 (not_14_out, In1);
  not not_15 (not_15_out, In0);
  not not_16 (not_16_out, s0);
  not not_17 (not_17_out, s2);
  not not_18 (not_18_out, In0);
  not not_19 (not_19_out, s2);
  not not_20 (not_20_out, s0);
  and and_1 (and_1_out, not_1_out, In1, In0);
  and and_2 (and_2_out, s1, In1);
  and and_3 (and_3_out, s1, s0, In0);
  and and_4 (and_4_out, s2, not_2_out, not_3_out);
  and and_5 (and_5_out, not_4_out, not_5_out, In1, not_6_out);
  and and_6 (and_6_out, not_7_out, not_8_out, s0, not_9_out, In0);
  and and_7 (and_7_out, not_10_out, s1, not_11_out, not_12_out);
  and and_8 (and_8_out, not_13_out, s1, not_14_out, not_15_out);
  and and_9 (and_9_out, not_16_out, In0);
  and and_10 (and_10_out, not_17_out, s0, not_18_out);
  and and_11 (and_11_out, not_19_out, s0, In1);
  and and_12 (and_12_out, s2, not_20_out, In1);
  or or_1 (Ns2, and_1_out, and_2_out, and_3_out, and_4_out);
  or or_2 (Ns1, and_5_out, and_6_out, and_7_out, and_8_out);
  or or_3 (Ns0, and_9_out, and_10_out, and_11_out, and_12_out);
endmodule

module change (
  input  s2,
  input  s1,
  input  s0,
  input  In1,
  input  In0,
  output change2,
  output change1,
  output change0
);

  wire and_3_out, and_4_out, not_1_out, not_2_out, not_3_out, not_4_out;

  not not_1 (not_1_out, s0);
  and and_1 (change1, s1, In1, In0);
  not not_2 (not_2_out, s2);
  not not_3 (not_3_out, s0);
  not not_4 (not_4_out, In0);
  and and_2 (change2, s2, not_1_out, In1, In0);
  and and_3 (and_3_out, not_2_out, s0, In1, In0);
  and and_4 (and_4_out, s2, not_3_out, In1, not_4_out);
  or or_1 (change0, and_3_out, and_4_out);
endmodule
