// Logisim project 算术右移1-未完成.circ as structural Verilog: 1 circuit, main circuit main
module main (
  input  [15:0] in_1,
  input  [3:0] in_2
);

  wire [15:0] demultiplexer_1_out0, demultiplexer_1_out1, or_1_out;

  Multiplexer #(.width(16), .enable("false")) multiplexer_1 ();  // open: in0, in1, out, sel
  Demultiplexer #(.width(16), .enable("false")) demultiplexer_1 (
    .out0(demultiplexer_1_out0), .out1(demultiplexer_1_out1), .in(in_1), .sel(in_2[0]));
  // Probe on demultiplexer_1_out0
  // Probe on {in_1[15], demultiplexer_1_out1[15:1]}
  assign or_1_out = {in_1[15], demultiplexer_1_out1[15:1]} | demultiplexer_1_out0;  // OR_Gate or_1, 16 bits wide
  // Probe on or_1_out

  // Other names for the same wires on the sheet: sign = in_1[15]
endmodule
