// Logisim project 算术右移2.circ as structural Verilog: 1 circuit, main circuit main
module main (
  input  [15:0] in_1,
  input  [3:0] in_2
);

  wire [15:0] multiplexer_1_out, multiplexer_2_out, multiplexer_3_out, multiplexer_4_out, shifter_1_out;

  Multiplexer #(.width(16), .enable("false")) multiplexer_1 (
    .in0(in_1), .in1({{2{in_1[15]}}, in_1[14:1]}), .out(multiplexer_1_out), .sel(in_2[0]));
  Multiplexer #(.width(16), .enable("false")) multiplexer_2 (
    .in0(multiplexer_1_out), .in1({{2{in_1[15]}}, multiplexer_1_out[15:2]}), .out(multiplexer_2_out),
    .sel(in_2[1]));
  Shifter #(.width(16), .shift("ar")) shifter_1 (.in(in_1), .\dist (in_2), .out(shifter_1_out));
  Multiplexer #(.width(16), .enable("false")) multiplexer_3 (
    .in0(multiplexer_2_out), .in1({{4{in_1[15]}}, multiplexer_2_out[15:4]}), .out(multiplexer_3_out),
    .sel(in_2[2]));
  // Probe on shifter_1_out
  // Probe on multiplexer_4_out
  Multiplexer #(.width(16), .enable("false")) multiplexer_4 (
    .in0(multiplexer_3_out), .in1({{8{in_1[15]}}, multiplexer_3_out[15:8]}), .out(multiplexer_4_out),
    .sel(in_2[3]));
  Comparator #(.width(16)) comparator_1 (.a(multiplexer_4_out), .b(shifter_1_out));  // open: gt, eq, lt

  // Other names for the same wires on the sheet: In[15:0] = in_1; sign = in_1[15]; Dis[3:0] = in_2
endmodule
