// Logisim project main.circ as structural Verilog
module main (
  input  in_1
);

  wire clk, undriven;
  wire [31:0] dm_1_rd, instr, RD1, RD2;

  Clock clock_1 (.out(clk));
  IFU ifu_1 (.reset(in_1), .clk(clk), .instr(instr));  // open: beq, eq, imm32
  GRF grf_1 (.RD1(RD1), .RD2(RD2), .clk(in_1), .reset(clk), .WE(undriven));  // open: A1, A2, A3, WD
  DM dm_1 (.clk(clk), .reset(in_1), .RD(dm_1_rd));  // open: A, WD, WE
  ALU alu_1 ();  // open: A, B, ALUop, eq, res

  // Other names for the same wires on the sheet: reset = in_1
endmodule

module GRF (
  input  clk,
  input  reset,
  input  WE,
  input  [4:0] A1,
  input  [4:0] A2,
  input  [4:0] A3,
  input  [31:0] WD,
  output [31:0] RD1,
  output [31:0] RD2
);

  wire [31:0] in00, in01, in02, in03, in04, in05, in06, in07, in08, in09, in10, in11, in12, in13, in14, in15,
       in16, in17, in18, in19, in20, in21, in22, in23, in24, in25, in26, in27, in28, in29, in30, in31, out00,
       out01, out02, out03, out04, out05, out06, out07, out08, out09, out10, out11, out12, out13, out14,
       out15, out16, out17, out18, out19, out20, out21, out22, out23, out24, out25, out26, out27, out28,
       out29, out30, out31;

  Demultiplexer #(.select(5), .width(32), .tristate("true"), .enable("false")) demultiplexer_1 (
    .out0(in00), .out1(in01), .out2(in02), .out3(in03), .out4(in04), .out5(in05), .out6(in06), .out7(in07),
    .out8(in08), .out9(in09), .out10(in10), .out11(in11), .out12(in12), .out13(in13), .out14(in14),
    .out15(in15), .out16(in16), .out17(in17), .out18(in18), .out19(in19), .out20(in20), .out21(in21),
    .out22(in22), .out23(in23), .out24(in24), .out25(in25), .out26(in26), .out27(in27), .out28(in28),
    .out29(in29), .out30(in30), .out31(in31), .in(WD), .sel(A3));
  Register #(.width(32)) register_1 (.D(in00), .Q(out00), .clr(1'b1));  // open: en, clk
  Register #(.width(32)) register_2 (.D(in08), .en(WE), .Q(out08), .clk(clk), .clr(reset));
  Register #(.width(32)) register_3 (.D(in16), .en(WE), .Q(out16), .clk(clk), .clr(reset));
  Register #(.width(32)) register_4 (.D(in24), .en(reset), .Q(out24), .clk(clk), .clr(reset));
  Register #(.width(32)) register_5 (.D(in01), .en(WE), .Q(out01), .clk(clk), .clr(reset));
  Register #(.width(32)) register_6 (.D(in09), .en(WE), .Q(out09), .clk(clk), .clr(reset));
  Register #(.width(32)) register_7 (.D(in17), .en(WE), .Q(out17), .clk(clk), .clr(reset));
  Register #(.width(32)) register_8 (.D(in25), .en(reset), .Q(out25), .clk(clk), .clr(reset));
  Multiplexer #(.select(5), .width(32), .enable("false")) multiplexer_1 (
    .in0(out00), .in1(out01), .in2(out02), .in3(out03), .in4(out04), .in5(out05), .in6(out06), .in7(out07),
    .in8(out08), .in9(out09), .in10(out10), .in11(out11), .in12(out12), .in13(out13), .in14(out14),
    .in15(out15), .in16(out16), .in17(out17), .in18(out18), .in19(out19), .in20(out20), .in21(out21),
    .in22(out22), .in23(out23), .in24(out24), .in25(out25), .in26(out26), .in27(out27), .in28(out28),
    .in29(out29), .in30(out30), .in31(out31), .out(RD1), .sel(A1));
  Register #(.width(32)) register_9 (.D(in02), .en(WE), .Q(out02), .clk(clk), .clr(reset));
  Register #(.width(32)) register_10 (.D(in10), .en(WE), .Q(out10), .clk(clk), .clr(reset));
  Register #(.width(32)) register_11 (.D(in18), .en(WE), .Q(out18), .clk(clk), .clr(reset));
  Register #(.width(32)) register_12 (.D(in26), .en(reset), .Q(out26), .clk(clk), .clr(reset));
  Register #(.width(32)) register_13 (.D(in03), .en(WE), .Q(out03), .clk(clk), .clr(reset));
  Register #(.width(32)) register_14 (.D(in11), .en(WE), .Q(out11), .clk(clk), .clr(reset));
  Register #(.width(32)) register_15 (.D(in19), .en(WE), .Q(out19), .clk(clk), .clr(reset));
  Register #(.width(32)) register_16 (.D(in27), .en(reset), .Q(out27), .clk(clk), .clr(reset));
  Register #(.width(32)) register_17 (.D(in04), .en(WE), .Q(out04), .clk(clk), .clr(reset));
  Register #(.width(32)) register_18 (.D(in12), .en(WE), .Q(out12), .clk(clk), .clr(reset));
  Register #(.width(32)) register_19 (.D(in20), .en(WE), .Q(out20), .clk(clk), .clr(reset));
  Register #(.width(32)) register_20 (.D(in28), .en(reset), .Q(out28), .clk(clk), .clr(reset));
  Multiplexer #(.select(5), .width(32), .enable("false")) multiplexer_2 (
    .in0(out00), .in1(out01), .in2(out02), .in3(out03), .in4(out04), .in5(out05), .in6(out06), .in7(out07),
    .in8(out08), .in9(out09), .in10(out10), .in11(out11), .in12(out12), .in13(out13), .in14(out14),
    .in15(out15), .in16(out16), .in17(out17), .in18(out18), .in19(out19), .in20(out20), .in21(out21),
    .in22(out22), .in23(out23), .in24(out24), .in25(out25), .in26(out26), .in27(out27), .in28(out28),
    .in29(out29), .in30(out30), .in31(out31), .out(RD2), .sel(A2));
  Register #(.width(32)) register_21 (.D(in05), .en(WE), .Q(out05), .clk(clk), .clr(reset));
  Register #(.width(32)) register_22 (.D(in13), .en(WE), .Q(out13), .clk(clk), .clr(reset));
  Register #(.width(32)) register_23 (.D(in21), .en(WE), .Q(out21), .clk(clk), .clr(reset));
  Register #(.width(32)) register_24 (.D(in29), .en(reset), .Q(out29), .clk(clk), .clr(reset));
  Register #(.width(32)) register_25 (.D(in06), .en(WE), .Q(out06), .clk(clk), .clr(reset));
  Register #(.width(32)) register_26 (.D(in14), .en(WE), .Q(out14), .clk(clk), .clr(reset));
  Register #(.width(32)) register_27 (.D(in22), .en(WE), .Q(out22), .clk(clk), .clr(reset));
  Register #(.width(32)) register_28 (.D(in30), .en(reset), .Q(out30), .clk(clk), .clr(reset));
  Register #(.width(32)) register_29 (.D(in07), .en(WE), .Q(out07), .clk(clk), .clr(reset));
  Register #(.width(32)) register_30 (.D(in15), .en(WE), .Q(out15), .clk(clk), .clr(reset));
  Register #(.width(32)) register_31 (.D(in23), .en(WE), .Q(out23), .clk(clk), .clr(reset));
  Register #(.width(32)) register_32 (.D(in31), .en(reset), .Q(out31), .clk(clk), .clr(reset));

  // Notes on the sheet:
  //   Global Register File
endmodule

module IFU (
  input  reset,
  input  clk,
  input  beq,
  input  eq,
  input  [31:0] imm32,
  output [31:0] instr
);

  wire and_1_out;
  wire [31:0] adder_1_out, NPC, PC, PC_4, shifter_1_out;

  Register #(.width(32)) u_PC (.D(NPC), .Q(PC), .clk(clk), .clr(reset));  // open: en
  Shifter #(.width(32)) shifter_1 (.in(imm32), .\dist (5'b00010), .out(shifter_1_out));
  Adder #(.width(32)) adder_1 (.a(PC_4), .b(shifter_1_out), .out(adder_1_out));  // open: cin, cout
  Adder #(.width(32)) adder_2 (.a(PC), .b(32'h4), .out(PC_4));  // open: cin, cout
  and and_1 (and_1_out, beq, eq);
  Multiplexer #(.width(32), .enable("false")) multiplexer_1 (.in0(PC_4), .in1(adder_1_out), .out(NPC), .sel(and_1_out));
  ROM #(.addrWidth(5), .dataWidth(32)) rom_1 (.addr(PC[6:2]), .data(instr));  // open: sel

  // Notes on the sheet:
  //   Instuction Fetch Unit
  //   contents of rom_1 (hex, n*v repeats v):
  //   0 1 2 3
endmodule

module ALU (
  input  [31:0] A,
  input  [31:0] B,
  input  [2:0] ALUop,
  output eq,
  output [31:0] res
);

  wire [31:0] adder_1_out, and_1_out, or_1_out, subtractor_1_out;

  Adder #(.width(32)) adder_1 (.a(A), .b(B), .out(adder_1_out));  // open: cin, cout
  Subtractor #(.width(32)) subtractor_1 (.a(A), .b(B), .out(subtractor_1_out));  // open: bin, bout
  assign and_1_out = A & B;  // AND_Gate and_1, 32 bits wide
  assign or_1_out = A | B;  // OR_Gate or_1, 32 bits wide
  Comparator #(.width(32)) comparator_1 (.a(B), .b(A), .eq(eq));  // open: gt, lt
  Multiplexer #(.select(3), .width(32), .enable("false")) multiplexer_1 (
    .in0(adder_1_out), .in1(subtractor_1_out), .in2(and_1_out), .in3(or_1_out), .out(res), .sel(ALUop));  // open: in4, in5, in6, in7

  // Notes on the sheet:
  //   Arithmetic and Logic Unit
endmodule

module EXT (
  input  [15:0] imm16,
  input  sign,
  output [31:0] imm32
);

  wire [31:0] bit_extender_1_out, bit_extender_2_out;

  assign bit_extender_1_out = {{16{imm16[15]}}, imm16};  // Bit_Extender bit_extender_1
  assign bit_extender_2_out = {{16{1'b0}}, imm16};  // Bit_Extender bit_extender_2
  Multiplexer #(.width(32), .enable("false")) multiplexer_1 (
    .in0(bit_extender_1_out), .in1(bit_extender_2_out), .out(imm32), .sel(sign));
endmodule

module DM (
  input  clk,
  input  reset,
  input  [4:0] A,
  input  [31:0] WD,
  input  WE,
  output [31:0] RD
);

  RAM #(.addrWidth(5), .dataWidth(32), .bus("separate")) ram_1 (
    .addr(A), .din(WD), .data(RD), .str(WE), .clk(clk), .clr(reset));  // open: sel, ld

  // Notes on the sheet:
  //   Data Memory
endmodule

module Controller (
  input  [5:0] Op,
  output WE_GRF,
  output WE_DM,
  output beq,
  output AluSrc,
  output out_6
);

  wire lui, lw, not_1_out, not_2_out, not_3_out, not_4_out, not_5_out, not_6_out, ori, R;

  // Probe on Op
  not not_1 (not_1_out, Op[0]);
  not not_2 (not_2_out, Op[1]);
  not not_3 (not_3_out, Op[2]);
  not not_4 (not_4_out, Op[3]);
  not not_5 (not_5_out, Op[4]);
  not not_6 (not_6_out, Op[5]);
  // Probe on nothing
  and u_R (R, not_1_out, not_2_out, not_3_out, not_4_out, not_5_out, not_6_out);
  and u_lw (lw, Op[0], Op[1], not_3_out, not_4_out, not_5_out, Op[5]);
  // AND_Gate and_1 is placed but not wired
  and sw (WE_DM, Op[0], Op[1], not_3_out, Op[3], not_5_out, Op[5]);
  or or_1 (WE_GRF, lw, R, ori, lui);
  and u_beq (beq, not_1_out, not_2_out, Op[2], not_4_out, not_5_out, not_6_out);
  and u_ori (ori, Op[0], not_2_out, Op[2], Op[3], not_5_out, not_6_out);
  and u_lui (lui, Op[0], Op[1], Op[2], Op[3], not_5_out, not_6_out);

  // Other names for the same wires on the sheet: sw = WE_DM

  // Notes on the sheet:
  //   Controller
endmodule
